// Logisim project PX16B.circ as structural Verilog: 2 circuits, main circuit main
// BGT
module main (
);

  wire AC0, AC1, AC2, ACALC, ACALCA, ACALCB, ADD, adder_1_cout, AIA, AIB, AND, and_1_out, and_2_out,
       and_3_out, and_4_out, and_5_out, and_6_out, and_7_out, and_9_out, and_10_out, and_12_out, and_13_out,
       and_18_out, and_19_out, and_21_out, and_22_out, and_24_out, and_25_out, and_26_out, and_27_out,
       and_28_out, and_29_out, and_31_out, and_32_out, and_34_out, and_35_out, and_37_out, and_38_out,
       and_39_out, and_40_out, and_42_out, and_43_out, and_44_out, and_49_out, and_50_out, and_51_out,
       and_53_out, and_56_out, and_66_out, and_67_out, and_68_out, and_69_out, and_70_out, and_71_out,
       and_73_out, and_74_out, and_75_out, and_76_out, APF, BCS, BEQ, BGT, BLT, BPF, buffer_3_out, CIN, CLI,
       CLOCK, CMP, comparator_1_lt, COUT, decoder_1_out0, decoder_1_out1, decoder_1_out2, decoder_1_out3,
       decoder_1_out4, decoder_1_out5, decoder_2_out0, decoder_2_out1, decoder_2_out2, decoder_2_out3,
       decoder_2_out4, decoder_2_out5, decoder_3_out0, decoder_3_out1, decoder_3_out2, decoder_3_out3,
       decoder_3_out4, decoder_3_out5, decoder_5_out4, decoder_6_out0, decoder_6_out1, decoder_6_out2,
       decoder_6_out3, decoder_6_out4, decoder_6_out5, decoder_6_out6, decoder_6_out7, decoder_6_out8,
       decoder_6_out9, decoder_6_out10, decoder_6_out11, decoder_6_out12, decoder_6_out13, decoder_6_out14,
       decoder_6_out15, DES, FCOUT, FNMI, FRIQ, FSCOUT, FZERO, HASA, HASB, I, IN0, INC, INS, JBC, JMP, JMPD,
       JMPQ, JSR, KPR, LD, LDM, LEA, LMAOPC, LOLPC, METH, nor_1_out, not_1_out, not_3_out, not_4_out,
       not_5_out, not_7_out, NPRA, NPRB, or_2_out, or_4_out, or_5_out, or_6_out, or_7_out, or_8_out,
       or_10_out, or_11_out, or_12_out, or_14_out, or_17_out, or_18_out, or_19_out, or_20_out, or_21_out,
       or_23_out, or_26_out, or_27_out, or_30_out, or_33_out, or_37_out, or_38_out, OUT0, OUT1, PEXEC0, PIE,
       PNMI, POFFS, POFFS0, POFFS1, POPJ, PPTR0, PPTR1, PRAM, PRB, PREINC, PSH, PSHJ, pull_resistor_7_node,
       pull_resistor_16_node, pull_resistor_18_node, pull_resistor_19_node, pull_resistor_20_node,
       pull_resistor_21_node, pull_resistor_22_node, pull_resistor_30_node, pull_resistor_33_node, QEXEC,
       QEXEC0, QINT0, QINT1, QLDA, QLDB, QNMI, QOFFS0, QPRA, QPRB, QPTR0, QRAM, RESET, RET, RTI, SADDR,
       SCOUT, SEI, SEXEC, shifter_1_carry_out, SHL, SIMM, SIMMA, SIMMB, SINT0, SINT1, SLDA, SLDB, SLDI,
       SOFFS, SPDA, SPDB, SPRA, SPRB, ST, STA, STB, STM, STPF, SUB, undriven, undriven_2, XOR, xor_7_out,
       ZERO;
  wire [1:0] controlled_buffer_39_out, MODA, MODB;
  wire [2:0] A, B;
  wire [2:2] and_47_out, pull_resistor_6_node;
  wire [4:2] PF_q;
  wire [7:0] and_36_out;
  wire [9:0] L_out;
  wire [12:11] PS_q, pull_resistor_1_node;
  wire [15:0] ABUS, ACBUS, adder_1_out, adder_3_out, ADDR0_q, bit_extender_1_out, bit_extender_2_out,
       bit_extender_3_out, bit_extender_4_out, controlled_buffer_1_out, controlled_buffer_3_out,
       controlled_buffer_41_out, DBUS, IMM0_q, IMM1_q, IR_q, IW, OFFS_q, or_3_out, PBUSA, PBUSB, PC_q, R0_q,
       R1_q, R2_q, R3_q, R4_q, ram_1_data, rom_1_data, shifter_1_out, ST_q, xor_1_out, xor_2_out, xor_3_out,
       xor_4_out, xor_5_out, xor_6_out;

  Comparator #(.width(16), .mode("unsigned")) comparator_1 (
    .a(ABUS), .b(16'h2000), .lt(comparator_1_lt));  // open: gt, eq
  not not_1 (not_1_out, comparator_1_lt);
  assign xor_1_out = PBUSA ^ bit_extender_2_out;  // XOR_Gate xor_1, 16 bits wide
  assign xor_2_out = PBUSB ^ bit_extender_1_out;  // XOR_Gate xor_2, 16 bits wide
  assign xor_3_out = PBUSA ^ 16'h8000;  // XOR_Gate xor_3, 16 bits wide
  assign xor_4_out = PBUSB ^ 16'h7fff;  // XOR_Gate xor_4, 16 bits wide
  or or_1 (INS, PSHJ, PSH);
  and and_1 (and_1_out, B[1], B[2]);
  Button L (.out(L_out[0]));
  or or_2 (or_2_out, IN0, STM, PSHJ);
  assign bit_extender_1_out = {{15{AIB}}, AIB};  // Bit_Extender bit_extender_1
  Adder #(.width(16)) adder_1 (.a(xor_1_out), .b(xor_2_out), .out(adder_1_out), .cin(CIN), .cout(adder_1_cout));
  assign xor_5_out = xor_1_out ^ xor_2_out;  // XOR_Gate xor_5, 16 bits wide
  assign or_3_out = xor_1_out | xor_2_out;  // OR_Gate or_3, 16 bits wide
  SHIFTER shifter_1 (
    .SHIFT_RIGHT(AC0), .ROTATE(AC1), .IN(xor_2_out), .OUT(shifter_1_out), .CARRY_IN(CIN),
    .CARRY_OUT(shifter_1_carry_out));
  Adder #(.width(16)) adder_2 (.a(xor_3_out), .b(xor_4_out), .cin(CIN), .cout(SCOUT));  // open: out
  Pull_Resistor pull_resistor_1 (.node({QNMI, QINT1, QINT0, pull_resistor_1_node, QEXEC0, QEXEC, POFFS0, QOFFS0, PPTR0, QPTR0, QRAM, QPRB, QPRA, QLDB, QLDA}));
  Register #(.width(16)) PS (
    .D({QNMI, QINT1, QINT0, pull_resistor_1_node, QEXEC0, QEXEC, POFFS0, QOFFS0, PPTR0, QPTR0, QRAM, QPRB, QPRA, QLDB, QLDA}),
    .Q({PNMI, SINT1, SINT0, PS_q, PEXEC0, SEXEC, POFFS1, POFFS0, PPTR1, PPTR0, PRAM, SPRB, SPRA, SLDB, SLDA}),
    .clk(CLOCK), .clr(RESET));  // open: en
  and and_2 (and_2_out, SEXEC, ~IW[4]);  // AND_Gate
  not not_2 (METH, IW[4]);
  nor nor_1 (nor_1_out, IW[2], IW[3]);
  and and_3 (and_3_out, ~IW[0], ~IW[1], IW[2], ~IW[3]);  // AND_Gate
  and and_4 (and_4_out, IW[0], ~IW[1], IW[2], ~IW[3]);  // AND_Gate
  and and_5 (and_5_out, IW[1], IW[2], ~IW[3]);  // AND_Gate
  and and_6 (and_6_out, ~IW[0], ~IW[2], IW[3]);  // AND_Gate
  and and_7 (and_7_out, IW[0], ~IW[1], ~IW[2], IW[3]);  // AND_Gate
  and and_8 (DES, INS, ~or_4_out);  // AND_Gate
  or or_4 (or_4_out, and_1_out, POPJ);
  Button U (.out(L_out[1]));
  Button R (.out(L_out[3]));
  Button D (.out(L_out[2]));
  Button SEL (.out(L_out[8]));
  Clock clock_1 (.out(CLOCK));
  Button button_1 (.out(RESET));
  assign controlled_buffer_1_out = comparator_1_lt ? rom_1_data : 16'bz;  // Controlled_Buffer controlled_buffer_1
  ROM #(.addrWidth(16), .dataWidth(16)) rom_1 (.addr(ABUS), .data(rom_1_data), .sel(comparator_1_lt));
  RAM #(.addrWidth(16), .dataWidth(16), .bus("separate")) ram_1 (
    .addr(ABUS), .din(DBUS), .data(ram_1_data), .str(or_2_out), .sel(not_1_out), .clk(CLOCK), .ld(not_1_out),
    .clr(RESET));
  assign controlled_buffer_1_out = not_1_out ? ram_1_data : 16'bz;  // Controlled_Buffer controlled_buffer_2
  assign bit_extender_2_out = {{15{AIA}}, AIA};  // Bit_Extender bit_extender_2
  assign controlled_buffer_3_out = ADD ? adder_1_out : 16'bz;  // Controlled_Buffer controlled_buffer_3
  assign COUT = ADD ? adder_1_cout : 1'bz;  // Controlled_Buffer controlled_buffer_4
  assign controlled_buffer_3_out = XOR ? xor_5_out : 16'bz;  // Controlled_Buffer controlled_buffer_5
  assign controlled_buffer_3_out = AND ? or_3_out : 16'bz;  // Controlled_Buffer controlled_buffer_6
  assign controlled_buffer_3_out = SHL ? shifter_1_out : 16'bz;  // Controlled_Buffer controlled_buffer_7
  assign COUT = SHL ? shifter_1_carry_out : 1'bz;  // Controlled_Buffer controlled_buffer_8
  and and_9 (and_9_out, HASA, A[2], A[1], A[0]);
  and and_10 (and_10_out, SLDI, ~and_9_out);  // AND_Gate
  and and_11 (QLDA, SLDI, and_9_out);
  and and_12 (and_12_out, and_2_out, nor_1_out);
  and and_13 (and_13_out, and_2_out, and_3_out);
  and and_14 (SHL, and_2_out, and_4_out);
  and and_15 (AND, and_2_out, and_5_out);
  and and_16 (CMP, and_2_out, and_6_out);
  and and_17 (XOR, and_2_out, and_7_out);
  Button X (.out(L_out[4]));
  Button START (.out(L_out[9]));
  assign DBUS = or_5_out ? controlled_buffer_1_out : 16'bz;  // Controlled_Buffer controlled_buffer_9
  or or_5 (or_5_out, LD, LDM);
  assign bit_extender_3_out = {{15{AIA}}, AIA};  // Bit_Extender bit_extender_3
  assign xor_6_out = bit_extender_3_out ^ controlled_buffer_3_out;  // XOR_Gate xor_6, 16 bits wide
  Pull_Resistor pull_resistor_2 (.node(COUT));
  Pull_Resistor pull_resistor_3 (.node(controlled_buffer_3_out));
  or or_6 (or_6_out, ADD, XOR, AND, SHL);
  Comparator #(.width(16), .mode("unsigned")) comparator_2 (
    .a(controlled_buffer_3_out), .b({16{1'b0}}), .eq(ZERO));  // open: gt, lt
  nor nor_2 (SLDI, SLDA, SLDB, SPRA, SPRB, PRAM, PPTR0, PPTR1, POFFS0, POFFS1, SEXEC, PEXEC0, SINT0, SINT1, PNMI);
  or or_7 (or_7_out, MODA[1], MODA[0]);
  and and_18 (and_18_out, HASA, or_7_out);
  or or_8 (or_8_out, SLDA, and_10_out);
  or or_9 (ADD, and_12_out, CMP, and_13_out);
  or or_10 (or_10_out, CMP, AND, and_12_out);
  or or_11 (or_11_out, SHL, and_13_out);
  Button Y (.out(L_out[5]));
  Button u_B (.out(L_out[6]));
  Button u_A (.out(L_out[7]));
  // Probe on DBUS
  Pull_Resistor pull_resistor_4 (.node(DBUS));
  assign DBUS = or_6_out ? xor_6_out : 16'bz;  // Controlled_Buffer controlled_buffer_10
  and and_19 (and_19_out, or_8_out, ~and_18_out);  // AND_Gate
  or or_12 (or_12_out, SPDA, and_19_out);
  and and_20 (NPRA, or_8_out, and_18_out);
  or or_13 (QPRA, NPRA, and_21_out);
  and and_21 (and_21_out, KPR, SPRA);
  and and_22 (and_22_out, B[0], or_11_out);
  and and_23 (AC1, B[1], or_11_out);
  and and_24 (and_24_out, B[2], or_11_out);
  and and_25 (and_25_out, IW[0], or_10_out);
  and and_26 (and_26_out, IW[1], or_10_out);
  Decoder #(.select(3), .disabled(0)) decoder_1 (
    .out0(decoder_1_out0), .out1(decoder_1_out1), .out2(decoder_1_out2), .out3(decoder_1_out3),
    .out4(decoder_1_out4), .out5(decoder_1_out5), .out6(STPF), .out7(IN0), .sel(A), .en(and_27_out));
  and and_27 (and_27_out, ST, ~SLDI);  // AND_Gate
  and and_28 (and_28_out, HASB, B[2], B[1], B[0]);
  and and_29 (and_29_out, or_12_out, ~and_28_out);  // AND_Gate
  and and_30 (QLDB, or_12_out, and_28_out);
  or or_14 (or_14_out, and_12_out, AND, CMP, XOR);
  or or_15 (AC0, and_22_out, and_25_out);
  or or_16 (AC2, and_24_out, and_26_out);
  or or_17 (or_17_out, DES, decoder_1_out5);
  assign DBUS = and_31_out ? PBUSA : 16'bz;  // Controlled_Buffer controlled_buffer_11
  and and_31 (and_31_out, STA, ~SLDI);  // AND_Gate
  assign and_36_out[5] = not_3_out ? FZERO : 1'bz;  // Controlled_Buffer controlled_buffer_12
  assign and_36_out[6] = not_3_out ? FSCOUT : 1'bz;  // Controlled_Buffer controlled_buffer_13
  assign and_36_out[7] = not_3_out ? FCOUT : 1'bz;  // Controlled_Buffer controlled_buffer_14
  not not_3 (not_3_out, METH);
  or or_18 (or_18_out, MODB[1], MODB[0]);
  and and_32 (and_32_out, HASB, or_18_out);
  or or_19 (or_19_out, SLDB, and_29_out);
  and and_33 (HASB, or_14_out, METH);
  buf buffer_1 (HASA, METH);
  assign PBUSB = decoder_3_out0 ? R0_q : 16'bz;  // Controlled_Buffer controlled_buffer_15
  Register #(.width(16)) R0 (.D(DBUS), .en(decoder_1_out0), .Q(R0_q), .clk(CLOCK), .clr(RESET));
  assign PBUSA = decoder_2_out0 ? R0_q : 16'bz;  // Controlled_Buffer controlled_buffer_16
  assign PBUSB = decoder_3_out1 ? R1_q : 16'bz;  // Controlled_Buffer controlled_buffer_17
  Register #(.width(16)) R1 (.D(DBUS), .en(decoder_1_out1), .Q(R1_q), .clk(CLOCK), .clr(RESET));
  assign PBUSA = decoder_2_out1 ? R1_q : 16'bz;  // Controlled_Buffer controlled_buffer_18
  assign PBUSB = decoder_3_out2 ? R2_q : 16'bz;  // Controlled_Buffer controlled_buffer_19
  Register #(.width(16)) R2 (.D(DBUS), .en(decoder_1_out2), .Q(R2_q), .clk(CLOCK), .clr(RESET));
  assign PBUSA = decoder_2_out2 ? R2_q : 16'bz;  // Controlled_Buffer controlled_buffer_20
  assign PBUSB = decoder_3_out3 ? R3_q : 16'bz;  // Controlled_Buffer controlled_buffer_21
  Register #(.width(16)) R3 (.D(DBUS), .en(decoder_1_out3), .Q(R3_q), .clk(CLOCK), .clr(RESET));
  assign PBUSA = decoder_2_out3 ? R3_q : 16'bz;  // Controlled_Buffer controlled_buffer_22
  assign PBUSB = decoder_3_out4 ? R4_q : 16'bz;  // Controlled_Buffer controlled_buffer_23
  Register #(.width(16)) R4 (.D(DBUS), .en(decoder_1_out4), .Q(R4_q), .clk(CLOCK), .clr(RESET));
  assign PBUSA = decoder_2_out4 ? R4_q : 16'bz;  // Controlled_Buffer controlled_buffer_24
  assign PBUSB = decoder_3_out5 ? ST_q : 16'bz;  // Controlled_Buffer controlled_buffer_25
  Counter #(.width(16), .max('hffff)) u_ST (
    .load(or_17_out), .D(DBUS), .count(INS), .Q(ST_q), .clk(CLOCK), .clr(RESET));  // open: carry
  assign PBUSA = decoder_2_out5 ? ST_q : 16'bz;  // Controlled_Buffer controlled_buffer_26
  assign ACBUS = INS ? ST_q : 16'bz;  // Controlled_Buffer controlled_buffer_27
  Decoder #(.select(3), .disabled(0)) decoder_2 (
    .out0(decoder_2_out0), .out1(decoder_2_out1), .out2(decoder_2_out2), .out3(decoder_2_out3),
    .out4(decoder_2_out4), .out5(decoder_2_out5), .out6(APF), .out7(OUT0), .sel(A), .en(and_34_out));
  and and_34 (and_34_out, HASA, ~SLDI);  // AND_Gate
  assign DBUS = and_35_out ? PBUSB : 16'bz;  // Controlled_Buffer controlled_buffer_28
  and and_35 (and_35_out, STB, ~SLDI);  // AND_Gate
  or or_20 (or_20_out, SEI, CLI, METH);
  and and_36 (and_36_out[0], ~CLI, or_21_out);  // AND_Gate
  or or_21 (or_21_out, SEI, FRIQ);
  or or_22 (and_36_out[1], SEI, FNMI);
  and and_37 (and_37_out, IW[15], FSCOUT);
  or or_23 (or_23_out, and_37_out, and_38_out);
  and and_38 (and_38_out, ~IW[15], FCOUT);  // AND_Gate
  and and_39 (and_39_out, BGT, and_43_out);
  Pull_Resistor pull_resistor_5 (.node(and_39_out));
  or or_24 (QEXEC, SPDB, QEXEC0, and_40_out);
  and and_40 (and_40_out, or_19_out, ~and_32_out);  // AND_Gate
  and and_41 (NPRB, or_19_out, and_32_out);
  or or_25 (QPRB, NPRB, and_42_out);
  and and_42 (and_42_out, KPR, SPRB);
  // Probe on IW[4:0]
  Pull_Resistor pull_resistor_6 (.node(pull_resistor_6_node[2]));
  assign pull_resistor_6_node[2] = SEXEC ? or_26_out : 1'bz;  // Controlled_Buffer controlled_buffer_29
  or or_26 (or_26_out, MODA[0], MODA[1]);
  Pull_Resistor pull_resistor_7 (.node(pull_resistor_7_node));
  assign pull_resistor_7_node = SEXEC ? or_27_out : 1'bz;  // Controlled_Buffer controlled_buffer_30
  or or_27 (or_27_out, MODB[0], MODB[1]);
  Register PF (.D(and_36_out), .en(or_20_out), .Q({FCOUT, FSCOUT, FZERO, PF_q, FNMI, FRIQ}), .clk(CLOCK), .clr(RESET));
  assign and_36_out[5] = METH ? COUT : 1'bz;  // Controlled_Buffer controlled_buffer_31
  assign and_36_out[6] = METH ? ZERO : 1'bz;  // Controlled_Buffer controlled_buffer_32
  assign and_36_out[7] = METH ? SCOUT : 1'bz;  // Controlled_Buffer controlled_buffer_33
  and and_43 (and_43_out, or_23_out, ~FZERO);  // AND_Gate
  and and_44 (and_44_out, ~or_23_out, ~FZERO);  // AND_Gate
  and and_45 (and_39_out, BLT, and_44_out);
  and and_46 (and_39_out, BEQ, FZERO);
  // Probe on B
  // Probe on A
  assign A = IW[7:5] | {3{pull_resistor_6_node[2]}};  // OR_Gate or_28, 3 bits wide
  assign B = IW[11:9] | {3{and_47_out[2]}};  // OR_Gate or_29, 3 bits wide
  and and_47 (and_47_out[2], pull_resistor_7_node, HASB);
  and and_48 (AIA, AND, ~AC0);  // AND_Gate
  and and_49 (and_49_out, AC0, ADD);
  and and_50 (and_50_out, AC2, FCOUT);
  Decoder #(.select(3), .disabled(0)) decoder_3 (
    .out0(decoder_3_out0), .out1(decoder_3_out1), .out2(decoder_3_out2), .out3(decoder_3_out3),
    .out4(decoder_3_out4), .out5(decoder_3_out5), .out6(BPF), .out7(OUT1), .sel(B), .en(and_51_out));
  and and_51 (and_51_out, HASB, ~SLDI);  // AND_Gate
  assign PBUSA = APF ? bit_extender_4_out : 16'bz;  // Controlled_Buffer controlled_buffer_34
  assign bit_extender_4_out = {{8{1'b0}}, {FCOUT, FSCOUT, FZERO, PF_q, FNMI, FRIQ}};  // Bit_Extender bit_extender_4
  assign PBUSB = BPF ? bit_extender_4_out : 16'bz;  // Controlled_Buffer controlled_buffer_35
  Pull_Resistor pull_resistor_8 (.node(and_36_out));
  and and_52 (and_39_out, BCS, or_23_out);
  xor xor_7 (xor_7_out, and_39_out, I);
  or or_30 (or_30_out, PRAM, PPTR1, POFFS1);
  // Probe on IW[14:13]
  LED led_1 (.in(IW[8]));
  or or_31 (SUB, CMP, and_49_out);
  and and_53 (and_53_out, SUB, ~and_50_out);  // AND_Gate
  or or_32 (CIN, and_53_out, and_50_out);
  and and_54 (CLI, B[0], SEI);
  and and_55 (JMPQ, or_33_out, SEXEC);
  or or_33 (or_33_out, JMPD, and_56_out);
  and and_56 (and_56_out, JBC, xor_7_out);
  or or_34 (KPR, PPTR0, POFFS0);
  and and_57 (SPDA, SPRA, or_30_out);
  and and_58 (SPDB, SPRB, or_30_out);
  LED led_2 (.in(IW[15]));
  LED led_3 (.in(I));
  assign MODA = not_4_out ? IW[14:13] : 2'bz;  // Controlled_Buffer controlled_buffer_36
  Pull_Resistor pull_resistor_9 (.node(MODA));
  not not_4 (not_4_out, IW[15]);
  assign MODB = IW[15] ? IW[14:13] : 2'bz;  // Controlled_Buffer controlled_buffer_37
  assign MODB = not_5_out ? 2'b00 : 2'bz;  // Controlled_Buffer controlled_buffer_38
  not not_5 (not_5_out, IW[15]);
  or or_35 (AIB, AIA, SUB);
  Pull_Resistor pull_resistor_10 (.node(PBUSB));
  Pull_Resistor pull_resistor_11 (.node(ABUS));
  Pull_Resistor pull_resistor_12 (.node(PBUSA));
  assign controlled_buffer_39_out = NPRA ? MODA : 2'bz;  // Controlled_Buffer controlled_buffer_39
  Pull_Resistor pull_resistor_13 (.node(controlled_buffer_39_out));
  assign controlled_buffer_39_out = NPRB ? MODB : 2'bz;  // Controlled_Buffer controlled_buffer_40
  Decoder #(.disabled(0)) decoder_4 (.out0(LDM), .out1(STM), .sel(DES), .en(PSH));
  Decoder #(.select(3), .disabled(0)) decoder_5 (
    .out0(BGT), .out1(BLT), .out2(BCS), .out3(BEQ), .out4(decoder_5_out4), .out5(JSR), .out6(RET),
    .out7(RTI), .sel(B), .en(JMP));
  not not_6 (JBC, B[2]);
  // Buffer buffer_2 has open pins: in=undriven, out=open
  and and_59 (QRAM, ~controlled_buffer_39_out[1], controlled_buffer_39_out[0]);  // AND_Gate
  and and_60 (QPTR0, controlled_buffer_39_out[1], ~controlled_buffer_39_out[0]);  // AND_Gate
  and and_61 (QOFFS0, controlled_buffer_39_out[1], controlled_buffer_39_out[0]);
  and and_62 (ACALCA, ~PRB, ACALC);  // AND_Gate
  and and_63 (ACALCB, PRB, ACALC);
  and and_64 (SIMMA, ~PRB, SIMM);  // AND_Gate
  and and_65 (SIMMB, PRB, SIMM);
  nor nor_3 (LOLPC, ACALC, INS, IN0);
  or or_36 (PRB, SLDB, SPRB);
  and and_66 (and_66_out, ~CMP, METH);  // AND_Gate
  Pull_Resistor pull_resistor_14 (.node(HASA));
  Pull_Resistor pull_resistor_15 (.node(HASB));
  Pull_Resistor pull_resistor_16 (.node(pull_resistor_16_node));
  buf buffer_3 (buffer_3_out, and_66_out);
  Pull_Resistor pull_resistor_17 (.node(buffer_3_out));
  buf buffer_4 (buffer_3_out, LDM);
  Pull_Resistor pull_resistor_18 (.node(pull_resistor_18_node));
  buf buffer_5 (pull_resistor_18_node, STM);
  Pull_Resistor pull_resistor_19 (.node(pull_resistor_19_node));
  Pull_Resistor pull_resistor_20 (.node(pull_resistor_20_node));
  Pull_Resistor pull_resistor_21 (.node(pull_resistor_21_node));
  Pull_Resistor pull_resistor_22 (.node(pull_resistor_22_node));
  LED led_4 (.in(decoder_6_out0));
  LED MATH (.in(and_66_out));
  assign controlled_buffer_41_out = ACALCA ? PBUSA : 16'bz;  // Controlled_Buffer controlled_buffer_41
  and and_67 (and_67_out, RTI, PEXEC0);
  Pull_Resistor pull_resistor_23 (.node(POPJ));
  Pull_Resistor pull_resistor_24 (.node(PSHJ));
  Pull_Resistor pull_resistor_25 (.node(QEXEC0));
  Pull_Resistor pull_resistor_26 (.node(LMAOPC));
  Pull_Resistor pull_resistor_27 (.node(JMPD));
  Decoder #(.select(4), .disabled(0)) decoder_6 (
    .out0(decoder_6_out0), .out1(decoder_6_out1), .out2(decoder_6_out2), .out3(decoder_6_out3),
    .out4(decoder_6_out4), .out5(decoder_6_out5), .out6(decoder_6_out6), .out7(decoder_6_out7),
    .out8(decoder_6_out8), .out9(decoder_6_out9), .out10(decoder_6_out10), .out11(decoder_6_out11),
    .out12(decoder_6_out12), .out13(decoder_6_out13), .out14(decoder_6_out14), .out15(decoder_6_out15),
    .sel(IW[3:0]), .en(IW[4]));
  LED led_5 (.in(decoder_6_out2));
  LED led_6 (.in(decoder_6_out4));
  LED led_7 (.in(decoder_6_out3));
  LED led_8 (.in(decoder_6_out1));
  Register #(.width(16)) IMM0 (.D(DBUS), .en(SIMMA), .Q(IMM0_q), .clk(CLOCK), .clr(RESET));
  and and_68 (and_68_out, OUT0, ~LMAOPC);  // AND_Gate
  Register #(.width(16)) ADDR0 (.D(ABUS), .en(SADDR), .Q(ADDR0_q), .clk(CLOCK), .clr(RESET));
  Register #(.width(16)) IMM1 (.D(DBUS), .en(SIMMB), .Q(IMM1_q), .clk(CLOCK), .clr(RESET));
  assign ACBUS = PIE ? PC_q : 16'bz;  // Controlled_Buffer controlled_buffer_42
  assign PBUSA = LMAOPC ? PC_q : 16'bz;  // Controlled_Buffer controlled_buffer_43
  Counter #(.width(16), .max('hffff)) PC (
    .load(JMPQ), .D(DBUS), .count(INC), .Q(PC_q), .clk(CLOCK), .clr(RESET));  // open: carry
  Pull_Resistor pull_resistor_28 (.node(ACBUS));
  Adder #(.width(16)) adder_3 (.a(ACBUS), .b(controlled_buffer_41_out), .out(adder_3_out), .cin(PREINC));  // open: cout
  assign controlled_buffer_41_out = ACALCB ? PBUSB : 16'bz;  // Controlled_Buffer controlled_buffer_44
  Pull_Resistor pull_resistor_29 (.node(controlled_buffer_41_out));
  not not_7 (not_7_out, SLDI);
  Register #(.width(16)) IR (.D(DBUS), .en(SLDI), .Q(IR_q), .clk(CLOCK), .clr(RESET));
  assign {IW[15:13], I, IW[11:0]} = not_7_out ? IR_q : 16'bz;  // Controlled_Buffer controlled_buffer_45
  assign {IW[15:13], I, IW[11:0]} = SLDI ? DBUS : 16'bz;  // Controlled_Buffer controlled_buffer_46
  Register #(.width(16)) OFFS (.D(DBUS), .en(SOFFS), .Q(OFFS_q), .clk(CLOCK), .clr(RESET));
  and and_69 (and_69_out, RET, PEXEC0);
  and and_70 (and_70_out, RTI, ~PEXEC0);  // AND_Gate
  and and_71 (and_71_out, JSR, PEXEC0);
  buf buffer_6 (JMPD, and_71_out);
  Pull_Resistor pull_resistor_30 (.node(pull_resistor_30_node));
  Pull_Resistor pull_resistor_31 (.node(INC));
  Pull_Resistor pull_resistor_32 (.node(LD));
  Pull_Resistor pull_resistor_33 (.node(pull_resistor_33_node));
  Pull_Resistor pull_resistor_34 (.node(ACALC));
  Pull_Resistor pull_resistor_35 (.node(SIMM));
  Pull_Resistor pull_resistor_36 (.node(POFFS));
  Pull_Resistor pull_resistor_37 (.node(SOFFS));
  buf buffer_7 (pull_resistor_30_node, PRAM);
  buf buffer_8 (pull_resistor_30_node, PPTR0);
  LED led_9 (.in(decoder_6_out8));
  LED led_10 (.in(decoder_6_out6));
  LED led_11 (.in(decoder_6_out5));
  LED led_12 (.in(decoder_6_out7));
  assign PBUSA = and_68_out ? IMM0_q : 16'bz;  // Controlled_Buffer controlled_buffer_47
  Pull_Resistor pull_resistor_38 (.node(ABUS));
  assign PBUSB = LEA ? ADDR0_q : 16'bz;  // Controlled_Buffer controlled_buffer_48
  assign ABUS = IN0 ? ADDR0_q : 16'bz;  // Controlled_Buffer controlled_buffer_49
  assign PBUSB = OUT1 ? IMM1_q : 16'bz;  // Controlled_Buffer controlled_buffer_50
  assign ABUS = LOLPC ? PC_q : 16'bz;  // Controlled_Buffer controlled_buffer_51
  assign ABUS = or_37_out ? adder_3_out : 16'bz;  // Controlled_Buffer controlled_buffer_52
  or or_37 (or_37_out, ACALC, INS);
  assign ACBUS = POFFS ? OFFS_q : 16'bz;  // Controlled_Buffer controlled_buffer_53
  and and_72 (PREINC, INS, ~DES);  // AND_Gate
  buf buffer_9 (JMPD, decoder_5_out4);
  and and_73 (and_73_out, JSR, ~PEXEC0);  // AND_Gate
  and and_74 (and_74_out, RET, ~PEXEC0);  // AND_Gate
  buf buffer_10 (POPJ, and_74_out);
  buf buffer_11 (PSHJ, and_73_out);
  buf buffer_12 (PSHJ, and_74_out);
  buf buffer_13 (QEXEC0, and_73_out);
  buf buffer_14 (LMAOPC, and_73_out);
  buf buffer_15 (JMPD, and_74_out);
  and and_75 (and_75_out, IW[8], ~PRB);  // AND_Gate
  and and_76 (and_76_out, I, PRB);
  buf buffer_16 (INC, SLDI);
  buf buffer_17 (LD, SLDI);
  buf buffer_18 (LD, SLDA);
  buf buffer_19 (INC, SLDA);
  buf buffer_20 (INC, SLDB);
  buf buffer_21 (LD, SLDB);
  buf buffer_22 (LD, PRAM);
  buf buffer_23 (pull_resistor_33_node, PRAM);
  buf buffer_24 (LD, PPTR0);
  buf buffer_25 (pull_resistor_33_node, PPTR0);
  buf buffer_26 (pull_resistor_33_node, PPTR1);
  buf buffer_27 (LD, PPTR1);
  buf buffer_28 (LD, POFFS0);
  buf buffer_29 (INC, POFFS0);
  buf buffer_30 (pull_resistor_33_node, POFFS1);
  buf buffer_31 (LD, POFFS1);
  buf buffer_32 (HASA, decoder_6_out11);
  buf buffer_33 (pull_resistor_18_node, decoder_6_out11);
  LED led_13 (.in(decoder_6_out10));
  LED MOV (.in(decoder_6_out12));
  LED u_JMP (.in(decoder_6_out11));
  LED u_SEI (.in(decoder_6_out9));
  and and_77 (SEI, decoder_6_out9, SEXEC);
  and and_78 (JMP, decoder_6_out11, SEXEC);
  or or_38 (or_38_out, and_75_out, and_76_out);
  and and_79 (PIE, or_38_out, pull_resistor_30_node);
  buf buffer_34 (SIMM, SLDA);
  buf buffer_35 (SIMM, SLDB);
  buf buffer_36 (ACALC, PRAM);
  buf buffer_37 (SIMM, PRAM);
  buf buffer_38 (ACALC, PPTR0);
  buf buffer_39 (SIMM, PPTR0);
  buf buffer_40 (SIMM, PPTR1);
  buf buffer_41 (ACALC, PPTR1);
  buf buffer_42 (SIMM, POFFS1);
  buf buffer_43 (ACALC, POFFS1);
  buf buffer_44 (POFFS, POFFS1);
  buf buffer_45 (HASA, decoder_6_out13);
  buf buffer_46 (HASA, decoder_6_out12);
  buf buffer_47 (HASA, decoder_6_out14);
  buf buffer_48 (HASB, decoder_6_out12);
  buf buffer_49 (HASB, decoder_6_out13);
  buf buffer_50 (pull_resistor_16_node, decoder_6_out13);
  buf buffer_51 (buffer_3_out, decoder_6_out13);
  buf buffer_52 (buffer_3_out, decoder_6_out12);
  buf buffer_53 (pull_resistor_19_node, decoder_6_out12);
  buf buffer_54 (pull_resistor_20_node, decoder_6_out14);
  LED u_PSH (.in(decoder_6_out14));
  LED u_LEA (.in(decoder_6_out13));
  LED HLT (.in(decoder_6_out15));
  DotMatrix #(.inputtype("row"), .matrixcols(16), .matrixrows(1), .dotshape("circle")) dotmatrix_1 (.row0(DBUS));
  DotMatrix #(.inputtype("row"), .matrixcols(16), .matrixrows(1), .dotshape("circle")) dotmatrix_2 (.row0(PBUSA));
  DotMatrix #(.inputtype("row"), .matrixcols(16), .matrixrows(1), .dotshape("circle")) dotmatrix_3 (.row0(PBUSB));
  DotMatrix #(.inputtype("row"), .matrixcols(16), .matrixrows(1), .dotshape("circle")) dotmatrix_4 (.row0(ABUS));
  DotMatrix #(.inputtype("row"), .matrixcols(16), .matrixrows(1), .dotshape("circle")) dotmatrix_5 (.row0(ACBUS));
  DotMatrix #(.inputtype("row"), .matrixcols(16), .matrixrows(1), .dotshape("circle")) dotmatrix_6 (.row0({IW[15:13], I, IW[11:0]}));
  and and_80 (SADDR, ~PRB, pull_resistor_33_node);  // AND_Gate
  LED led_14 (.in(SLDI));
  LED led_15 (.in(SLDA));
  LED led_16 (.in(SPRA));
  LED led_17 (.in(SLDB));
  LED led_18 (.in(SPRB));
  LED led_19 (.in(PRAM));
  LED led_20 (.in(PPTR0));
  LED led_21 (.in(PPTR1));
  LED led_22 (.in(POFFS0));
  buf buffer_55 (SOFFS, POFFS0);
  LED led_23 (.in(POFFS1));
  LED led_24 (.in(SEXEC));
  LED led_25 (.in(SINT0));
  LED led_26 (.in(SINT1));
  and and_81 (LEA, SEXEC, pull_resistor_16_node);
  and and_82 (ST, SEXEC, buffer_3_out);
  and and_83 (STA, SEXEC, pull_resistor_18_node);
  and and_84 (STB, SEXEC, pull_resistor_19_node);
  and and_85 (PSH, SEXEC, pull_resistor_20_node);
  // Buffer buffer_56 has open pins: in=undriven_2, out=open

  // Other names for the same wires on the sheet: QPTR1 = PPTR0; QOFFS1 = POFFS0; AIO = AIA; C[2:0] = B;
  //   O[4:0] = IW[4:0]; NORMIE = IW[4]; P = IW[8]; IW[12] = I; Q = I; X[1:0] = IW[14:13]; S = IW[15]; Y = IW[15];
  //   ROT = AC1; SHR = AC0

  // Notes on the sheet:
  //   ROMLEN
  //   ARITHMETIC AND LOGIC UNIT
  //   INSTRUCTION LOADING
  //   INSTRUCTION DECODING
  //   CONTROLLER
  //   contents of rom_1 (hex, n*v repeats v):
  //   ebc ffff afb 10 1f 11*0 fe feca ca c3e c1b
  //   FLAGS REGISTER
  //   BRANCHING UNIT
  //   and_33 drives only 1 and floats otherwise
  //   buffer_1 drives only 1 and floats otherwise
  //   and_39 drives only 1 and floats otherwise
  //   and_45 drives only 1 and floats otherwise
  //   and_46 drives only 1 and floats otherwise
  //   and_52 drives only 1 and floats otherwise
  //   FLOW CONTROL UNIT
  //   buffer_2 drives only 1 and floats otherwise
  //   buffer_3 drives only 1 and floats otherwise
  //   buffer_4 drives only 1 and floats otherwise
  //   buffer_5 drives only 1 and floats otherwise
  //   buffer_6 drives only 1 and floats otherwise
  //   buffer_7 drives only 1 and floats otherwise
  //   buffer_8 drives only 1 and floats otherwise
  //   buffer_9 drives only 1 and floats otherwise
  //   buffer_10 drives only 1 and floats otherwise
  //   buffer_11 drives only 1 and floats otherwise
  //   buffer_12 drives only 1 and floats otherwise
  //   buffer_13 drives only 1 and floats otherwise
  //   buffer_14 drives only 1 and floats otherwise
  //   buffer_15 drives only 1 and floats otherwise
  //   buffer_16 drives only 1 and floats otherwise
  //   buffer_17 drives only 1 and floats otherwise
  //   buffer_18 drives only 1 and floats otherwise
  //   buffer_19 drives only 1 and floats otherwise
  //   buffer_20 drives only 1 and floats otherwise
  //   buffer_21 drives only 1 and floats otherwise
  //   buffer_22 drives only 1 and floats otherwise
  //   buffer_23 drives only 1 and floats otherwise
  //   buffer_24 drives only 1 and floats otherwise
  //   buffer_25 drives only 1 and floats otherwise
  //   buffer_26 drives only 1 and floats otherwise
  //   buffer_27 drives only 1 and floats otherwise
  //   buffer_28 drives only 1 and floats otherwise
  //   buffer_29 drives only 1 and floats otherwise
  //   buffer_30 drives only 1 and floats otherwise
  //   buffer_31 drives only 1 and floats otherwise
  //   buffer_32 drives only 1 and floats otherwise
  //   buffer_33 drives only 1 and floats otherwise
  //   buffer_34 drives only 1 and floats otherwise
  //   buffer_35 drives only 1 and floats otherwise
  //   buffer_36 drives only 1 and floats otherwise
  //   buffer_37 drives only 1 and floats otherwise
  //   buffer_38 drives only 1 and floats otherwise
  //   buffer_39 drives only 1 and floats otherwise
  //   buffer_40 drives only 1 and floats otherwise
  //   buffer_41 drives only 1 and floats otherwise
  //   buffer_42 drives only 1 and floats otherwise
  //   buffer_43 drives only 1 and floats otherwise
  //   buffer_44 drives only 1 and floats otherwise
  //   buffer_45 drives only 1 and floats otherwise
  //   buffer_46 drives only 1 and floats otherwise
  //   buffer_47 drives only 1 and floats otherwise
  //   buffer_48 drives only 1 and floats otherwise
  //   buffer_49 drives only 1 and floats otherwise
  //   buffer_50 drives only 1 and floats otherwise
  //   buffer_51 drives only 1 and floats otherwise
  //   buffer_52 drives only 1 and floats otherwise
  //   buffer_53 drives only 1 and floats otherwise
  //   buffer_54 drives only 1 and floats otherwise
  //   buffer_55 drives only 1 and floats otherwise
  //   buffer_56 drives only 1 and floats otherwise
endmodule

module SHIFTER (
  input  ROTATE,
  input  CARRY_IN,
  input  SHIFT_RIGHT,
  input  [15:0] IN,
  output [15:0] OUT,
  output CARRY_OUT
);

  wire and_1_out, not_1_out;
  wire [0:0] or_1_out;

  or or_1 (or_1_out[0], CARRY_IN, and_1_out);
  and and_1 (and_1_out, ROTATE, CARRY_OUT);
  assign OUT = SHIFT_RIGHT ? {IN[14:0], or_1_out[0]} : 16'bz;  // Controlled_Buffer controlled_buffer_1
  assign CARRY_OUT = SHIFT_RIGHT ? IN[15] : 1'bz;  // Controlled_Buffer controlled_buffer_2
  assign CARRY_OUT = not_1_out ? IN[0] : 1'bz;  // Controlled_Buffer controlled_buffer_3
  assign OUT = not_1_out ? {or_1_out[0], IN[15:1]} : 16'bz;  // Controlled_Buffer controlled_buffer_4
  not not_1 (not_1_out, SHIFT_RIGHT);
endmodule
