// Logisim project PX16C.circ as structural Verilog: 1 circuit, main circuit main
module main (
);

  wire AADD, Act, adder_1_cout, Addr, AIA, AIB, and_1_p1, and_1_p2, and_2_out, and_3_out, and_4_out,
       and_5_p2, and_6_out, and_7_out, and_8_p3, and_9_out, and_11_out, and_12_p2, and_12_p6, and_13_p5,
       and_14_p3, and_15_out, and_16_p2, and_17_out, and_19_p3, AOR, ASHL, ASHR, AXA, AXB, AXOR, Boot_0,
       Boot_1, button_2_out, Cin, CLK, clock_2_out, CMP, comparator_2_lt, Cond_met, Cout, decoder_1_out0,
       decoder_1_out1, decoder_1_out2, decoder_1_out3, decoder_1_out4, decoder_1_out6, decoder_1_out7,
       decoder_2_out0, decoder_2_out1, decoder_2_out2, decoder_2_out3, decoder_2_out4, decoder_2_out5,
       decoder_2_out6, decoder_2_out7, decoder_3_out0, decoder_3_out1, decoder_3_out2, decoder_3_out3,
       decoder_3_out4, decoder_3_out5, decoder_3_out6, decoder_4_out0, decoder_4_out1, decoder_4_out4,
       demultiplexer_1_out0, demultiplexer_1_out1, demultiplexer_2_out0, demultiplexer_2_out1,
       demultiplexer_3_out0, demultiplexer_4_out1, demultiplexer_5_out0, demultiplexer_5_out1,
       demultiplexer_6_out1, demultiplexer_7_out1, demultiplexer_8_out1, demultiplexer_9_out0,
       demultiplexer_9_out1, demultiplexer_11_out0, demultiplexer_11_out1, Flag_Cout, Flag_SCout, Flag_Zero,
       INC, IRQ_Enable, Is_JSR, Is_LEA, Is_ST, IY, Jsr, Load_0, Load_1, Load_2, Mov, multiplexer_6_out,
       multiplexer_9_out, multiplexer_10_out, multiplexer_11_out, nand_1_p2, nand_1_p4, nand_2_out,
       nand_3_out, nand_4_out, NMI_Enable, nor_2_p2, nor_3_out, not_1_out, not_2_out, not_3_out, not_4_out,
       not_5_out, not_7_out, not_8_out, not_9_out, not_10_out, not_11_out, or_3_out, or_4_p2, or_5_p2,
       or_6_out, or_7_out, or_8_out, or_9_out, or_11_out, or_15_p3, or_16_out, or_19_p3, or_20_p3, or_21_out,
       or_23_out, or_24_p2, or_25_out, or_33_out, Pop, Push, R4, R6, RM, Rp, RST, SAr, SCout, Si0, Si1,
       undriven, WM, WPF, WR, xor_7_p4, xor_8_out, Zero;
  wire [0:0] PS_q, xor_1_out;
  wire [2:0] A, B, D, IA, IB, IX, multiplexer_3_out, multiplexer_4_out, multiplexer_7_out, multiplexer_8_out;
  wire [2:2] or_18_out;
  wire [5:0] IOp;
  wire [6:0] controlled_buffer_20_out, keyboard_1_data;
  wire [10:2] or_17_out;
  wire [12:2] PF, pull_resistor_3_node;
  wire [14:0] xor_1_out_2;
  wire [15:0] Ab, adder_1_out, AR_q, bit_extender_1_out, bit_extender_2_out, bit_extender_3_out,
       controlled_buffer_18_out, controlled_buffer_19_out, Db, imm0_q, imm1_q, multiplexer_2_out, or_2_p3,
       PbA, PbB, PC_q, R0_q, R1_q, R2_q, R3_q, ram_1_data, Rb, rom_1_data, ST_q, xor_2_out, xor_3_out,
       xor_4_out, xor_5_out, xor_6_out;

  // Probe on PbA
  DotMatrix #(.inputtype("row"), .matrixcols(8), .matrixrows(2), .dotshape("circle")) dotmatrix_1 (
    .row0(PbA[15:8]), .row1(PbA[7:0]));
  // Probe on PbB
  DotMatrix #(.inputtype("row"), .matrixcols(8), .matrixrows(2), .dotshape("circle")) dotmatrix_2 (
    .row0(PbB[15:8]), .row1(PbB[7:0]));
  // Probe on Rb
  DotMatrix #(.inputtype("row"), .matrixcols(8), .matrixrows(2), .dotshape("circle")) dotmatrix_3 (
    .row0(Rb[15:8]), .row1(Rb[7:0]));
  // Probe on Db
  DotMatrix #(.inputtype("row"), .matrixcols(8), .matrixrows(2), .dotshape("circle")) dotmatrix_4 (
    .row0(Db[15:8]), .row1(Db[7:0]));
  // Probe on Ab
  DotMatrix #(.inputtype("row"), .matrixcols(8), .matrixrows(2), .dotshape("circle")) dotmatrix_5 (
    .row0(Ab[15:8]), .row1(Ab[7:0]));
  // Probe on PbA
  // Probe on PbB
  // Probe on Rb
  // Probe on Db
  // Probe on Ab
  or or_1 (WM, decoder_1_out7, decoder_1_out7);
  Button button_1 (.out(RST));
  Clock clock_1 (.out(CLK));
  Decoder #(.select(3), .disabled(0), .enable("true")) decoder_1 (
    .out0(decoder_1_out0), .out1(decoder_1_out1), .out2(decoder_1_out2), .out3(decoder_1_out3),
    .out4(decoder_1_out4), .out5(WPF), .out6(decoder_1_out6), .out7(decoder_1_out7), .sel(D), .en(WR));
  DotMatrix #(.matrixcols(32), .matrixrows(16), .dotshape("circle")) dotmatrix_6 ();  // open: col0, col1, col2, col3, col4, col5, col6, col7, col8, col9, col10, col11, col12, col13, col14, col15, col16, col17, col18, col19, col20, col21, col22, col23, col24, col25, col26, col27, col28, col29, col30, col31
  Register #(.width(16)) R0 (.D(Db), .en(decoder_1_out0), .Q(R0_q), .clk(CLK), .clr(RST));
  Register #(.width(16)) R1 (.D(Db), .en(decoder_1_out1), .Q(R1_q), .clk(CLK), .clr(RST));
  Register #(.width(16)) R2 (.D(Db), .en(decoder_1_out2), .Q(R2_q), .clk(CLK), .clr(RST));
  Register #(.width(16)) R3 (.D(Db), .en(decoder_1_out3), .Q(R3_q), .clk(CLK), .clr(RST));
  Register #(.width(16)) ST (.D(Db), .en(decoder_1_out4), .Q(ST_q), .clk(CLK), .clr(RST));
  Counter #(.width(16), .max('hffff)) PC (
    .load(decoder_1_out6), .D(Db), .count(INC), .Q(PC_q), .clk(CLK), .clr(RST));  // open: carry
  Register #(.width(16)) imm0 (.D(Db), .en(Si0), .Q(imm0_q), .clk(CLK), .clr(RST));
  Register #(.width(16)) imm1 (.D(Db), .en(Si1), .Q(imm1_q), .clk(CLK), .clr(RST));
  assign PbA = decoder_2_out0 ? R0_q : 16'bz;  // Controlled_Buffer controlled_buffer_1
  assign PbB = decoder_3_out0 ? R0_q : 16'bz;  // Controlled_Buffer controlled_buffer_2
  assign PbA = decoder_2_out1 ? R1_q : 16'bz;  // Controlled_Buffer controlled_buffer_3
  assign PbB = decoder_3_out1 ? R1_q : 16'bz;  // Controlled_Buffer controlled_buffer_4
  assign PbA = decoder_2_out2 ? R2_q : 16'bz;  // Controlled_Buffer controlled_buffer_5
  assign PbB = decoder_3_out2 ? R2_q : 16'bz;  // Controlled_Buffer controlled_buffer_6
  assign PbA = decoder_2_out3 ? R3_q : 16'bz;  // Controlled_Buffer controlled_buffer_7
  assign PbB = decoder_3_out3 ? R3_q : 16'bz;  // Controlled_Buffer controlled_buffer_8
  assign PbA = decoder_2_out4 ? ST_q : 16'bz;  // Controlled_Buffer controlled_buffer_9
  assign PbB = decoder_3_out4 ? ST_q : 16'bz;  // Controlled_Buffer controlled_buffer_10
  assign PbA = decoder_2_out5 ? {Flag_SCout, Flag_Cout, Flag_Zero, PF, IRQ_Enable, NMI_Enable} : 16'bz;  // Controlled_Buffer controlled_buffer_11
  assign PbB = decoder_3_out5 ? {Flag_SCout, Flag_Cout, Flag_Zero, PF, IRQ_Enable, NMI_Enable} : 16'bz;  // Controlled_Buffer controlled_buffer_12
  assign PbA = decoder_2_out6 ? PC_q : 16'bz;  // Controlled_Buffer controlled_buffer_13
  assign PbB = decoder_3_out6 ? PC_q : 16'bz;  // Controlled_Buffer controlled_buffer_14
  assign PbA = decoder_2_out7 ? imm0_q : 16'bz;  // Controlled_Buffer controlled_buffer_15
  assign PbB = and_2_out ? imm0_q : 16'bz;  // Controlled_Buffer controlled_buffer_16
  assign PbB = and_1_p1 ? imm1_q : 16'bz;  // Controlled_Buffer controlled_buffer_17
  // AND_Gate and_1: pin names not known; wires that end beside it: and_1_p1, and_1_p2
  Decoder #(.select(3), .disabled(0)) decoder_2 (
    .out0(decoder_2_out0), .out1(decoder_2_out1), .out2(decoder_2_out2), .out3(decoder_2_out3),
    .out4(decoder_2_out4), .out5(decoder_2_out5), .out6(decoder_2_out6), .out7(decoder_2_out7), .sel(A),
    .en(and_2_out));
  and and_2 (and_2_out, IA[0], IA[1], IA[2], ~IY, Addr);  // AND_Gate
  Decoder #(.select(3), .disabled(0)) decoder_3 (
    .out0(decoder_3_out0), .out1(decoder_3_out1), .out2(decoder_3_out2), .out3(decoder_3_out3),
    .out4(decoder_3_out4), .out5(decoder_3_out5), .out6(decoder_3_out6), .out7(and_1_p2), .sel(B));  // open: en
  Clock clock_2 (.out(clock_2_out));
  Button button_2 (.out(button_2_out));
  TTY tty_1 (.data(controlled_buffer_20_out), .clk(clock_2_out), .we(1'b0), .clr(button_2_out));
  Keyboard keyboard_1 (.clk(clock_2_out), .re(1'b0), .clr(button_2_out), .data(keyboard_1_data));  // open: avail
  assign controlled_buffer_18_out = not_2_out ? PbA : 16'bz;  // Controlled_Buffer controlled_buffer_18
  assign controlled_buffer_19_out = not_1_out ? PbB : 16'bz;  // Controlled_Buffer controlled_buffer_19
  not not_1 (not_1_out, AXB);
  not not_2 (not_2_out, AXA);
  Register #(.width(16)) AR (.D(Rb), .en(SAr), .Q(AR_q), .clk(CLK), .clr(RST));
  assign controlled_buffer_20_out = 1'b0 ? keyboard_1_data : 7'bz;  // Controlled_Buffer controlled_buffer_20
  assign controlled_buffer_18_out = AXA ? {16{1'b0}} : 16'bz;  // Controlled_Buffer controlled_buffer_21
  assign controlled_buffer_19_out = AXB ? {16{1'b0}} : 16'bz;  // Controlled_Buffer controlled_buffer_22
  assign bit_extender_1_out = {{15{AIB}}, AIB};  // Bit_Extender bit_extender_1
  assign bit_extender_2_out = {{15{AIA}}, AIA};  // Bit_Extender bit_extender_2
  assign bit_extender_3_out = {{15{AIA}}, AIA};  // Bit_Extender bit_extender_3
  Comparator #(.width(16), .mode("unsigned")) comparator_1 (.a({16{1'b0}}), .b(Rb), .eq(Zero));  // open: gt, lt
  Pull_Resistor pull_resistor_1 (.node(Rb));
  Multiplexer #(.width(16)) multiplexer_1 (.in0(Rb), .in1(AR_q), .out(Ab), .sel(WM));  // open: en
  not not_3 (not_3_out, RM);
  assign Db = not_3_out ? Rb : 16'bz;  // Controlled_Buffer controlled_buffer_23
  ExactlyOne xor_1[15:0] (
    .out({xor_1_out_2, xor_1_out[0]}), .in1(controlled_buffer_18_out), .in3(bit_extender_2_out),
    .in4(controlled_buffer_19_out));
  ExactlyOne xor_2[15:0] (
    .out(xor_2_out), .in0(bit_extender_2_out), .in1(controlled_buffer_19_out), .in3(bit_extender_1_out));
  Adder #(.width(16)) adder_1 (
    .a({xor_1_out_2, xor_1_out[0]}), .b(xor_2_out), .out(adder_1_out), .cin(Cin), .cout(adder_1_cout));
  ExactlyOne xor_3[15:0] (.out(xor_3_out), .in1({xor_1_out_2, xor_1_out[0]}), .in3(16'h8000), .in4(xor_2_out));
  Adder #(.width(16)) adder_2 (.a(xor_3_out), .b(xor_4_out), .cin(Cin), .cout(SCout));  // open: out
  ExactlyOne xor_4[15:0] (.out(xor_4_out), .in0(16'h8000), .in1(xor_2_out), .in3(16'h8000));
  assign xor_5_out = {xor_1_out_2, xor_1_out[0]} ^ xor_2_out;  // XOR_Gate xor_5, 16 bits wide
  // OR_Gate #(.width(16)) or_2: pin names not known; wires that end beside it: {xor_1_out_2, xor_1_out[0]}, xor_2_out, or_2_p3
  assign xor_6_out = or_2_p3 ^ bit_extender_3_out;  // XOR_Gate xor_6, 16 bits wide
  ROM #(.addrWidth(16), .dataWidth(16)) rom_1 (.addr(Ab), .data(rom_1_data), .sel(1'b1));
  RAM #(.addrWidth(16), .dataWidth(16)) ram_1 (
    .addr(Ab), .data(ram_1_data), .sel(1'b1), .clk(and_3_out), .ld(and_5_p2), .clr(RST));
  and and_3 (and_3_out, CLK, WM);
  Comparator #(.width(16), .mode("unsigned")) comparator_2 (.a(Ab), .b(16'h20), .lt(comparator_2_lt));  // open: gt, eq
  assign Rb = AADD ? adder_1_out : 16'bz;  // Controlled_Buffer controlled_buffer_24
  assign Cout = AADD ? adder_1_cout : 1'bz;  // Controlled_Buffer controlled_buffer_25
  Pull_Resistor pull_resistor_2 (.node(Cout));
  assign Rb = AXOR ? xor_5_out : 16'bz;  // Controlled_Buffer controlled_buffer_26
  assign Rb = AOR ? xor_6_out : 16'bz;  // Controlled_Buffer controlled_buffer_27
  assign Rb = ASHL ? {xor_1_out_2[13:0], xor_1_out[0], Cin} : 16'bz;  // Controlled_Buffer controlled_buffer_28
  assign Cout = ASHL ? xor_1_out_2[14] : 1'bz;  // Controlled_Buffer controlled_buffer_29
  assign Rb = ASHR ? {Cin, xor_1_out_2} : 16'bz;  // Controlled_Buffer controlled_buffer_30
  assign Cout = ASHR ? xor_1_out[0] : 1'bz;  // Controlled_Buffer controlled_buffer_31
  assign Db = and_4_out ? rom_1_data : 16'bz;  // Controlled_Buffer controlled_buffer_32
  assign ram_1_data = WM ? Db : 16'bz;  // Controlled_Buffer controlled_buffer_33
  assign Db = and_5_p2 ? ram_1_data : 16'bz;  // Controlled_Buffer controlled_buffer_34
  and and_4 (and_4_out, RM, comparator_2_lt, RM);
  // AND_Gate and_5: pin names not known; wires that end beside it: comparator_2_lt, and_5_p2
  Pull_Resistor pull_resistor_3 (.node({SCout, Cout, Zero, pull_resistor_3_node, IRQ_Enable, NMI_Enable}));
  Multiplexer #(.width(16)) multiplexer_2 (
    .in0({SCout, Cout, Zero, pull_resistor_3_node, IRQ_Enable, NMI_Enable}), .in1(Db),
    .out(multiplexer_2_out), .sel(WPF), .en(undriven));
  or or_3 (or_3_out, undriven, WPF, Act);
  Register #(.width(16)) u_PF (
    .D(multiplexer_2_out), .en(or_3_out), .Q({Flag_SCout, Flag_Cout, Flag_Zero, PF, IRQ_Enable, NMI_Enable}),
    .clk(CLK), .clr(RST));
  not not_4 (not_4_out, Load_0);
  Demultiplexer #(.disabled(0)) demultiplexer_1 (
    .out0(demultiplexer_1_out0), .out1(demultiplexer_1_out1), .in(Addr), .sel(IY));
  // NAND_Gate nand_1: pin names not known; wires that end beside it: IX[0], nand_1_p2, IX[2], nand_1_p4
  and and_6 (and_6_out, ~multiplexer_3_out[0], ~multiplexer_3_out[1], multiplexer_3_out[2]);  // AND_Gate
  Multiplexer #(.width(3)) multiplexer_3 (
    .in0(Db[11:9]), .in1(3'b111), .out(multiplexer_3_out), .sel(not_4_out));  // open: en
  // OR_Gate or_4: pin names not known; wires that end beside it: demultiplexer_1_out1, or_4_p2, Load_0
  Multiplexer #(.width(3)) multiplexer_4 (
    .in0(Db[8:6]), .in1(3'b111), .out(multiplexer_4_out), .sel(not_4_out));  // open: en
  // OR_Gate or_5: pin names not known; wires that end beside it: demultiplexer_1_out0, or_5_p2, Load_0
  and and_7 (and_7_out, Addr, nand_1_p4);
  or or_6 (or_6_out, Boot_0, Boot_1, Pop);
  Decoder #(.select(3), .disabled(0), .enable("true")) decoder_4 (
    .out0(decoder_4_out0), .out1(decoder_4_out1), .out2(CMP), .out3(AIA), .out4(decoder_4_out4), .out5(AXOR),
    .out6(ASHL), .out7(ASHR), .sel(IOp[2:0]), .en(Act));
  or or_7 (or_7_out, Push, or_6_out);
  Register #(.width(1)) Y (.D(Db[15]), .en(Load_0), .Q(IY), .clk(CLK), .clr(RST));
  Register #(.width(3)) X (.D(Db[14:12]), .en(Load_0), .Q(IX), .clk(CLK), .clr(RST));
  Register #(.width(3)) u_B (.D(multiplexer_3_out), .en(or_4_p2), .Q(IB), .clk(CLK), .clr(RST));
  Register #(.width(3)) u_A (.D(multiplexer_4_out), .en(or_5_p2), .Q(IA), .clk(CLK), .clr(RST));
  Register #(.width(6)) Opcode (.D(Db[5:0]), .en(Load_0), .Q(IOp), .clk(CLK), .clr(RST));
  Register #(.width(1)) Y_2 (.D(and_6_out), .en(Load_0), .Q(Is_ST), .clk(CLK), .clr(RST));
  or or_8 (or_8_out, and_7_out, or_6_out, decoder_4_out0);
  // AND_Gate and_8: pin names not known; wires that end beside it: IOp[4], Act, and_8_p3
  or or_9 (or_9_out, decoder_4_out1, Push, CMP);
  not not_5 (not_5_out, or_8_out);
  or or_10 (AXB, and_8_p3, or_7_out, or_7_out);
  or or_11 (or_11_out, or_7_out, or_7_out, Act);
  Register #(.width(11), .trigger("falling")) PS (
    .D({or_17_out, Boot_0, 1'b1}),
    .Q({Pop, Mov, Act, Addr, Jsr, Push, Load_2, Load_1, Load_0, Boot_1, PS_q[0]}), .clk(CLK), .clr(RST));  // open: en
  nor nor_1 (AXA, Act, Push, or_8_out);
  or or_12 (AADD, AXA, or_8_out, or_9_out);
  // OR_Gate or_13: pin names not known; wires that end beside it: or_9_out, AIA, AIB
  // OR_Gate or_14: pin names not known; wires that end beside it: or_9_out, AIA, decoder_4_out4, AOR
  // XOR_Gate xor_7: pin names not known; wires that end beside it: not_5_out, AXB, Flag_Cout, xor_7_p4
  Multiplexer #(.disabled(0), .enable("true")) multiplexer_5 (
    .in0(xor_7_p4), .in1(Flag_Cout), .out(Cin), .sel(IOp[3]), .en(or_11_out));
  not not_6 (Boot_0, PS_q[0]);
  Demultiplexer #(.disabled(0)) demultiplexer_2 (
    .out0(demultiplexer_2_out0), .out1(demultiplexer_2_out1), .in(multiplexer_6_out), .sel(not_7_out));  // open: en
  not not_7 (not_7_out, IY);
  and and_9 (and_9_out, ~IA[0], ~IA[1], IA[2]);  // AND_Gate
  Multiplexer #(.disabled(0), .enable("true")) multiplexer_6 (
    .in0(and_9_out), .in1(Is_ST), .out(multiplexer_6_out), .sel(IY), .en(nand_2_out));
  nand nand_2 (nand_2_out, IX[0], IX[1], IX[2]);
  // OR_Gate or_15: pin names not known; wires that end beside it: Boot_1, Pop, or_15_p3
  or or_16 (or_16_out, Act, Mov);
  Demultiplexer #(.disabled(0)) demultiplexer_3 (
    .out0(demultiplexer_3_out0), .out1(or_17_out[10]), .in(or_16_out), .sel(demultiplexer_2_out0));  // open: en
  or or_17 (or_17_out[2], or_15_p3, demultiplexer_5_out1, demultiplexer_3_out0);
  Demultiplexer #(.disabled(0)) demultiplexer_4 (
    .out0(or_17_out[3]), .out1(demultiplexer_4_out1), .in(Load_0), .sel(nand_3_out));
  Demultiplexer #(.disabled(0)) demultiplexer_5 (
    .out0(demultiplexer_5_out0), .out1(demultiplexer_5_out1), .in(Addr), .sel(Is_LEA));  // open: en
  not not_8 (not_8_out, nand_2_out);
  nand nand_3 (nand_3_out, IA[0], IA[1], IA[2]);
  nand nand_4 (nand_4_out, IB[0], IB[1], IB[2]);
  or or_18 (or_18_out[2], R6, R4);
  Multiplexer #(.width(3), .disabled(0)) multiplexer_7 (
    .in0(IA), .in1(IB), .out(multiplexer_7_out), .sel(IY));  // open: en
  // OR_Gate or_19: pin names not known; wires that end beside it: demultiplexer_4_out1, Load_1, or_19_p3
  Demultiplexer #(.disabled(0)) demultiplexer_6 (
    .out0(or_17_out[4]), .out1(demultiplexer_6_out1), .in(or_19_p3), .sel(nand_4_out));
  // OR_Gate or_20: pin names not known; wires that end beside it: demultiplexer_6_out1, Load_2, or_20_p3
  Demultiplexer #(.disabled(0)) demultiplexer_7 (
    .out0(or_17_out[5]), .out1(demultiplexer_7_out1), .in(or_20_p3), .sel(nor_2_p2));  // open: en
  // NOR_Gate nor_2: pin names not known; wires that end beside it: demultiplexer_2_out1, nor_2_p2, Is_JSR
  Multiplexer #(.width(3), .disabled(0)) multiplexer_8 (
    .in0(multiplexer_7_out), .in1(IB), .out(multiplexer_8_out), .sel(Mov));  // open: en
  Demultiplexer #(.disabled(0)) demultiplexer_8 (
    .out0(or_17_out[6]), .out1(demultiplexer_8_out1), .in(Push), .sel(not_9_out));  // open: en
  or or_21 (or_21_out, Jsr, Jsr, demultiplexer_7_out1);
  Demultiplexer #(.disabled(0)) demultiplexer_9 (
    .out0(demultiplexer_9_out0), .out1(demultiplexer_9_out1), .in(or_21_out), .sel(not_8_out));  // open: en
  not not_9 (not_9_out, Is_JSR);
  and and_10 (Is_LEA, IOp[4], IOp[4], IOp[5]);
  assign A = or_18_out[2] ? {or_18_out[2], R6, 1'b0} : 3'bz;  // Controlled_Buffer controlled_buffer_35
  Pull_Resistor pull_resistor_4 (.node(A));
  assign A = Addr ? IX : 3'bz;  // Controlled_Buffer controlled_buffer_36
  assign A = Rp ? IA : 3'bz;  // Controlled_Buffer controlled_buffer_37
  assign B = or_18_out[2] ? {or_18_out[2], R6, 1'b0} : 3'bz;  // Controlled_Buffer controlled_buffer_38
  assign B = Addr ? multiplexer_8_out : 3'bz;  // Controlled_Buffer controlled_buffer_39
  Pull_Resistor pull_resistor_5 (.node(B));
  assign B = Rp ? IB : 3'bz;  // Controlled_Buffer controlled_buffer_40
  assign D = or_18_out[2] ? {or_18_out[2], R6, 1'b0} : 3'bz;  // Controlled_Buffer controlled_buffer_41
  assign D = Addr ? IA : 3'bz;  // Controlled_Buffer controlled_buffer_42
  Pull_Resistor pull_resistor_6 (.node(D));
  assign D = Rp ? IA : 3'bz;  // Controlled_Buffer controlled_buffer_43
  or or_22 (or_17_out[7], demultiplexer_8_out1, demultiplexer_9_out0);
  Demultiplexer #(.disabled(0)) demultiplexer_10 (
    .out0(or_17_out[8]), .out1(or_17_out[9]), .in(or_23_out), .sel(IOp[5]));  // open: en
  or or_23 (or_23_out, demultiplexer_9_out1, demultiplexer_5_out0);
  Multiplexer multiplexer_9 (.in0(Flag_Cout), .in1(Flag_SCout), .out(multiplexer_9_out), .sel(IOp[1]));  // open: en
  and and_11 (and_11_out, Addr, Is_LEA);
  // AND_Gate and_12: pin names not known; wires that end beside it: multiplexer_9_out, and_12_p2, multiplexer_9_out, Flag_Zero, Flag_Zero, and_12_p6
  // AND_Gate and_13: pin names not known; wires that end beside it: Flag_Zero, and_12_p2, multiplexer_9_out, multiplexer_9_out, and_13_p5
  nor nor_3 (nor_3_out, IOp[5], and_11_out, Mov);
  // OR_Gate or_24: pin names not known; wires that end beside it: Pop, or_24_p2, Push
  // AND_Gate and_14: pin names not known; wires that end beside it: Addr, Is_LEA, and_14_p3
  and and_15 (and_15_out, IX[0], IX[1], IX[2]);
  Multiplexer #(.select(2), .disabled(0)) multiplexer_10 (
    .in0(and_12_p6), .in1(and_13_p5), .in2(Flag_Zero), .in3(multiplexer_9_out), .out(multiplexer_10_out),
    .sel({IOp[2], IOp[0]}));  // open: en
  not not_10 (not_10_out, IOp[3]);
  // AND_Gate and_16: pin names not known; wires that end beside it: IOp[1], and_16_p2, IOp[2]
  buf and_17 (and_17_out, ~Addr);  // AND_Gate AND_Gate
  Multiplexer multiplexer_11 (
    .in0(multiplexer_10_out), .in1(not_10_out), .out(multiplexer_11_out), .sel(and_16_p2));  // open: en
  and and_18 (Is_JSR, ~IOp[0], IOp[1], IOp[2], IOp[3], IOp[5]);  // AND_Gate
  or or_25 (or_25_out, Boot_0, Boot_1, Load_0);
  // OR_Gate or_26: pin names not known; wires that end beside it: Load_1, Load_1, Load_2, INC
  Demultiplexer #(.disabled(0), .enable("true")) demultiplexer_11 (
    .out0(demultiplexer_11_out0), .out1(demultiplexer_11_out1), .in(Addr), .sel(IY), .en(not_11_out));
  not not_11 (not_11_out, and_14_p3);
  // AND_Gate and_19: pin names not known; wires that end beside it: CMP, Act, and_19_p3
  ExactlyOne xor_8 (.out(xor_8_out), .in1(multiplexer_11_out), .in3(IOp[3]), .in4(IOp[3]));
  or or_27 (Cond_met, xor_8_out, nor_3_out);
  or or_28 (R6, INC, or_25_out, Jsr);
  // OR_Gate or_29: pin names not known; wires that end beside it: Load_1, demultiplexer_11_out0, Si0
  // OR_Gate or_30: pin names not known; wires that end beside it: Load_2, demultiplexer_11_out1, Si1
  // OR_Gate or_31: pin names not known; wires that end beside it: Push, Pop, R4
  or or_32 (RM, INC, Boot_1, and_17_out);
  or or_33 (or_33_out, or_25_out, Mov, and_14_p3, or_24_p2, and_19_p3);
  // OR_Gate or_34: pin names not known; wires that end beside it: Addr, Push, SAr
  or or_35 (Rp, Mov, Act);
  and and_20 (WR, or_33_out, Cond_met);
  // also tied to GND on the sheet: {controlled_buffer_20_out[1], controlled_buffer_20_out[2], controlled_buffer_20_out[3], controlled_buffer_20_out[4]}
  // also tied to VCC on the sheet: {controlled_buffer_20_out[0], controlled_buffer_20_out[5], controlled_buffer_20_out[6]}

  // Other names for the same wires on the sheet: PF (some bits) = {Flag_SCout, Flag_Cout, Flag_Zero, IRQ_Enable, NMI_Enable};
  //   Ra = Addr

  // Notes on the sheet:
  //   PbA
  //   PbB
  //   Rb
  //   Db
  //   Ab
  //   Registers file
  //   Arithmetic And Logic unit
  //   SHL
  //   SHR
  //   Memory
  //   contents of rom_1 (hex, n*v repeats v):
  //   ffff ffff 3 7f26 ffff 7e26 15 7e66 b 7fae c 7191 7485 7012 dfb8 17 7017 dfbd 14 7280 7056 dfb6 d
  //   7426 d9a6
  //   Flags register
  //   ALU decoder
  //   Instruction unpacker
  //   ADD
  //   SUB
  //   CMP
  //   AND
  //   OR
  //   XOR
  //   SHL
  //   SHR
  //   CC
  //   MATH1
  //   State machine
  //   PASS
  //   Register decoder
  //   Condition decoder
  //   Miscellaneous decoders
  //   LT
  //   GT
  //   EQ
  //   CS
endmodule
