// Logisim project PX16C.circ as structural Verilog: 3 circuits, main circuit main
module main (
);

  wire A_out, AADD, Act, adder_1_cout, adder_2_cout, adder_3_cout, adder_5_cout, Addr, AIA, AIB, and_3_out,
       and_4_p1, and_4_p2, and_5_out, and_6_out, and_7_p3, and_8_p3, and_10_p3, and_11_p4, and_12_p5,
       and_13_p6, and_14_p6, and_15_p5, and_16_out, and_17_p3, and_18_out, and_19_p3, and_20_out, and_21_out,
       and_23_out, and_24_out, and_25_out, and_27_out, and_28_out, and_30_p1, and_30_p2, and_34_out,
       and_35_p1, and_37_out, and_38_p2, and_38_p6, and_39_p5, and_40_p4, and_42_out, and_44_p2, and_46_p3,
       and_47_p3, and_48_out, AOR, ASHL, ASHR, AXA, AXB, AXOR, B_out, Boot_0, Boot_1, buffer_5_out,
       button_2_out, button_3_out, button_4_out, button_5_out, button_6_out, Button_Ack, CCLK, Cin,
       clock_1_out, CMP, comparator_1_lt, comparator_2_gt, comparator_3_eq, comparator_4_eq, comparator_5_eq,
       comparator_6_eq, comparator_6_gt, comparator_6_lt, comparator_8_eq, comparator_8_gt, comparator_8_lt,
       comparator_9_eq, comparator_9_gt, comparator_9_lt, comparator_10_eq, comparator_10_gt,
       comparator_10_lt, comparator_11_eq, comparator_12_eq, comparator_13_eq, comparator_14_eq,
       comparator_15_eq, comparator_16_eq, Cond_met, Cout, CPUCE, CRST, CX, decoder_1_out0, decoder_1_out1,
       decoder_1_out2, decoder_1_out3, decoder_1_out4, decoder_1_out6, decoder_2_out0, decoder_2_out1,
       decoder_2_out2, decoder_2_out3, decoder_2_out4, decoder_2_out5, decoder_2_out6, decoder_2_out7,
       decoder_3_out0, decoder_3_out1, decoder_3_out2, decoder_3_out3, decoder_3_out4, decoder_3_out5,
       decoder_3_out6, decoder_4_out0, decoder_4_out1, decoder_4_out4, demultiplexer_2_out0,
       demultiplexer_3_out0, demultiplexer_3_out1, demultiplexer_4_out1, demultiplexer_5_out0,
       demultiplexer_5_out1, demultiplexer_6_out1, demultiplexer_7_out1, demultiplexer_9_out1,
       demultiplexer_10_out0, demultiplexer_10_out1, demultiplexer_12_out0, demultiplexer_12_out1, Flag_Cout,
       Flag_SCout, Flag_Zero, INC, INT_prog, INT_soft, Intr_0, Intr_1, Intr_2, Intr_3, Intr_4, IRQ,
       IRQ_Enable, Is_CX, Is_INTR, Is_JSR, Is_LEA, Is_ST, IY, Jsr, Load_0, Load_1, Load_2, MCLK, Mov, MRST,
       multiplexer_3_out, multiplexer_11_out, multiplexer_16_out, multiplexer_17_out, multiplexer_18_out,
       nand_1_p2, nand_1_p4, nand_2_out, nand_3_out, nand_4_out, NMI, NMI_Enable, No_Button_Wake,
       No_Timer_Wake, nor_2_p2, nor_3_out, not_2_out, not_4_out, not_6_out, not_7_out, not_8_out, not_9_out,
       not_10_out, not_11_out, not_12_out, not_13_out, not_14_out, not_16_out, not_17_out, not_18_out,
       not_19_out, not_20_out, or_1_p4, or_2_p1, or_5_out, or_6_out, or_7_out, or_8_out, or_9_out, or_11_out,
       or_12_p1, or_12_p2, or_13_p1, or_13_p2, or_14_out, or_15_out, or_18_out, or_19_out, or_20_out,
       or_21_out, or_24_p3, or_25_p3, or_26_out, or_27_out, or_28_out, or_30_out, or_31_out, or_32_p2,
       or_32_p3, or_33_out, or_34_out, or_35_p3, or_36_out, or_38_out, or_39_out, or_43_out, or_44_out,
       or_51_out, Pop, Push, R4, R6, RbC, register_1_q, RM, Rp, RRST, SAr, SCout, Screen_Disable, Sel_out,
       Si0, Si1, Sleep_Deep, Sleep_Idle, Sleep_Light, Sta_out, TCLK, Timer_Ack, Timer_Enable, Timer_IRQ,
       Timer_NMI, Timer_Read, Timer_Write, v_out, Wake, WM, WPF, WR, WR7, X_out, xor_7_p4, xor_8_out, Y_out,
       Zero;
  wire [0:0] Divisor_31_0_q, PS_q;
  wire [2:0] A, B, D, IA, IB, IX, multiplexer_8_out, multiplexer_9_out, multiplexer_14_out,
       multiplexer_15_out, Sleep_q;
  wire [2:2] or_22_out;
  wire [5:0] IOp;
  wire [6:0] keyboard_1_data;
  wire [7:0] Limit_q, pull_resistor_9_node;
  wire [7:3] Mode_q;
  wire [7:7] controlled_buffer_42_out;
  wire [11:2] demultiplexer_8_out0;
  wire [12:4] PF, pull_resistor_12_node;
  wire [15:0] Ab, adder_5_out, and_41_out, AR, bit_extender_1_out, bit_extender_2_out, bit_extender_3_out,
       bit_extender_4_out, button_inputs_1_data_out, controlled_buffer_19_out, controlled_buffer_21_out,
       controlled_buffer_22_out, controlled_buffer_28_out, counter_1_q, Db, imm0, imm1, Limit_High_q,
       Limit_Low_q, multiplexer_7_out, multiplexer_12_out, multiplexer_13_out,
       n32x16_screen_controller_1_col_0, n32x16_screen_controller_1_col_1, n32x16_screen_controller_1_col_2,
       n32x16_screen_controller_1_col_3, n32x16_screen_controller_1_col_4, n32x16_screen_controller_1_col_5,
       n32x16_screen_controller_1_col_6, n32x16_screen_controller_1_col_7, n32x16_screen_controller_1_col_8,
       n32x16_screen_controller_1_col_9, n32x16_screen_controller_1_col_10,
       n32x16_screen_controller_1_col_11, n32x16_screen_controller_1_col_12,
       n32x16_screen_controller_1_col_13, n32x16_screen_controller_1_col_14,
       n32x16_screen_controller_1_col_15, n32x16_screen_controller_1_col_16,
       n32x16_screen_controller_1_col_17, n32x16_screen_controller_1_col_18,
       n32x16_screen_controller_1_col_19, n32x16_screen_controller_1_col_20,
       n32x16_screen_controller_1_col_21, n32x16_screen_controller_1_col_22,
       n32x16_screen_controller_1_col_23, n32x16_screen_controller_1_col_24,
       n32x16_screen_controller_1_col_25, n32x16_screen_controller_1_col_26,
       n32x16_screen_controller_1_col_27, n32x16_screen_controller_1_col_28,
       n32x16_screen_controller_1_col_29, n32x16_screen_controller_1_col_30,
       n32x16_screen_controller_1_col_31, not_1_out, or_3_p3, or_4_out, PbA, PbB, PC, pull_resistor_11_node,
       R0, R1, R2, R3, Rb, rom_1_data, ST, Temp_High_q, Temp_Low_q, Timer_q, Timer_q_2, xor_1_out, xor_2_out,
       xor_3_out, xor_4_out, xor_5_out, xor_6_out;
  wire [30:0] Divisor_94_63_q, Divisor_126_95_q;
  wire [31:0] Accumulator_31_0_q, adder_1_out, adder_2_out, adder_3_out, adder_4_out, and_9_out,
       Divisor_31_0_q_2, Divisor_94_63_q_2, multiplexer_1_out, multiplexer_2_out, multiplexer_4_out,
       multiplexer_5_out, not_3_out, not_5_out, pull_resistor_5_node, pull_resistor_6_node,
       pull_resistor_7_node, pull_resistor_8_node, Remainder_31_0_q, Remainder_63_32_q;
  wire [31:31] Accumulator_63_32_q;

  // Probe on R0
  DotMatrix #(.inputtype("row"), .matrixcols(8), .matrixrows(2), .dotshape("circle")) dotmatrix_1 (
    .row0(R0[15:8]), .row1(R0[7:0]));
  // Probe on R1
  DotMatrix #(.inputtype("row"), .matrixcols(8), .matrixrows(2), .dotshape("circle")) dotmatrix_2 (
    .row0(R1[15:8]), .row1(R1[7:0]));
  // Probe on R2
  DotMatrix #(.inputtype("row"), .matrixcols(8), .matrixrows(2), .dotshape("circle")) dotmatrix_3 (
    .row0(R2[15:8]), .row1(R2[7:0]));
  // Probe on R3
  DotMatrix #(.inputtype("row"), .matrixcols(8), .matrixrows(2), .dotshape("circle")) dotmatrix_4 (
    .row0(R3[15:8]), .row1(R3[7:0]));
  // Probe on ST
  DotMatrix #(.inputtype("row"), .matrixcols(8), .matrixrows(2), .dotshape("circle")) dotmatrix_5 (
    .row0(ST[15:8]), .row1(ST[7:0]));
  // Probe on {Flag_SCout, Flag_Cout, Flag_Zero, PF, INT_prog, INT_soft, IRQ_Enable, NMI_Enable}
  DotMatrix #(.inputtype("row"), .matrixcols(8), .matrixrows(2), .dotshape("circle")) dotmatrix_6 (
    .row0({Flag_SCout, Flag_Cout, Flag_Zero, PF[12:8]}),
    .row1({PF[7:4], INT_prog, INT_soft, IRQ_Enable, NMI_Enable}));
  // Probe on PC
  DotMatrix #(.inputtype("row"), .matrixcols(8), .matrixrows(2), .dotshape("circle")) dotmatrix_7 (
    .row0(PC[15:8]), .row1(PC[7:0]));
  // Probe on R0
  // Probe on R1
  // Probe on R2
  // Probe on R3
  // Probe on ST
  // Probe on {Flag_SCout, Flag_Cout, Flag_Zero, PF, INT_prog, INT_soft, IRQ_Enable, NMI_Enable}
  // Probe on PC
  Button button_1 (.out(MRST));
  Clock clock_1 (.out(clock_1_out));
  Pull_Resistor pull_resistor_1 (.node(IRQ));
  Pull_Resistor pull_resistor_2 (.node(NMI));
  // Probe on counter_1_q
  Counter #(.width(16), .max('hffff)) counter_1 (.Q(counter_1_q), .clk(CCLK));  // open: load, D, count, carry, clr
  buf buffer_1 (IRQ, 1'b0);
  buf buffer_2 (NMI, 1'b0);
  // AND_Gate and_1: pin names not known; wires that end beside it: MRST, clock_1_out, MCLK
  // Probe on PbA
  // Probe on PbA
  DotMatrix #(.inputtype("row"), .matrixcols(8), .matrixrows(2), .dotshape("circle")) dotmatrix_8 (
    .row0(PbA[15:8]), .row1(PbA[7:0]));
  // Probe on PbB
  // Probe on PbB
  DotMatrix #(.inputtype("row"), .matrixcols(8), .matrixrows(2), .dotshape("circle")) dotmatrix_9 (
    .row0(PbB[15:8]), .row1(PbB[7:0]));
  // Probe on AR
  // Probe on AR
  DotMatrix #(.inputtype("row"), .matrixcols(8), .matrixrows(2), .dotshape("circle")) dotmatrix_10 (
    .row0(AR[15:8]), .row1(AR[7:0]));
  // Probe on Db
  // Probe on Db
  DotMatrix #(.inputtype("row"), .matrixcols(8), .matrixrows(2), .dotshape("circle")) dotmatrix_11 (
    .row0(Db[15:8]), .row1(Db[7:0]));
  // Probe on Ab
  // Probe on Ab
  DotMatrix #(.inputtype("row"), .matrixcols(8), .matrixrows(2), .dotshape("circle")) dotmatrix_12 (
    .row0(Ab[15:8]), .row1(Ab[7:0]));
  // Probe on imm0
  // Probe on imm0
  DotMatrix #(.inputtype("row"), .matrixcols(8), .matrixrows(2), .dotshape("circle")) dotmatrix_13 (
    .row0(imm0[15:8]), .row1(imm0[7:0]));
  // Probe on imm1
  // Probe on imm1
  DotMatrix #(.inputtype("row"), .matrixcols(8), .matrixrows(2), .dotshape("circle")) dotmatrix_14 (
    .row0(imm1[15:8]), .row1(imm1[7:0]));
  and and_2 (CCLK, CPUCE, MCLK);
  buf buffer_3 (CRST, MRST);
  Pull_Resistor pull_resistor_3 (.node(CRST));
  Decoder #(.select(3), .disabled(0), .enable("true")) decoder_1 (
    .out0(decoder_1_out0), .out1(decoder_1_out1), .out2(decoder_1_out2), .out3(decoder_1_out3),
    .out4(decoder_1_out4), .out5(WPF), .out6(decoder_1_out6), .out7(WR7), .sel(D), .en(WR));
  assign not_1_out = ~16'h20;  // NOT_Gate not_1, 16 bits wide
  Pull_Resistor pull_resistor_4 (.node(RRST));
  buf buffer_4 (RRST, MRST);
  Button button_2 (.out(button_2_out));
  Button button_3 (.out(button_3_out));
  and and_3 (and_3_out, CCLK, WM);
  Comparator #(.width(16), .mode("unsigned")) comparator_1 (
    .a(Ab), .b(16'h2000), .lt(comparator_1_lt));  // open: gt, eq
  Comparator #(.width(16), .mode("unsigned")) comparator_2 (
    .a(Ab), .b(not_1_out), .gt(comparator_2_gt));  // open: eq, lt
  Register #(.width(32)) Accumulator_31_0 (
    .D(and_9_out), .en(1'b1), .Q({Accumulator_31_0_q[0], and_9_out[31:1]}), .clk(button_3_out),
    .clr(button_2_out));
  Register #(.width(32)) Accumulator_63_32 (
    .D(Accumulator_31_0_q), .en(1'b1), .Q({Accumulator_63_32_q[31], Accumulator_31_0_q[31:1]}),
    .clk(button_3_out), .clr(button_2_out));
  Register #(.width(32)) Remainder_31_0 (
    .D(multiplexer_1_out), .en(1'b1), .Q(Remainder_31_0_q), .clk(button_3_out), .clr(button_2_out));
  Register #(.width(32)) Remainder_63_32 (
    .D(multiplexer_2_out), .en(1'b1), .Q(Remainder_63_32_q), .clk(button_3_out), .clr(button_2_out));
  Register #(.width(32)) Divisor_31_0 (
    .D(Divisor_31_0_q_2), .en(1'b1), .Q({Divisor_31_0_q_2[30:0], Divisor_31_0_q[0]}), .clk(button_3_out),
    .clr(button_2_out));
  Register #(.width(31)) Divisor_62_32 (
    .D(Divisor_94_63_q), .en(1'b1), .Q({Divisor_94_63_q[29:0], Divisor_31_0_q_2[31]}), .clk(button_3_out),
    .clr(button_2_out));
  Register #(.width(32)) Divisor_94_63 (
    .D(Divisor_94_63_q_2), .en(1'b1), .Q({Divisor_94_63_q_2[30:0], Divisor_94_63_q[30]}), .clk(button_3_out),
    .clr(button_2_out));
  Register #(.width(32)) Divisor_126_95 (
    .D({1'b0, Divisor_126_95_q}), .en(1'b1), .Q({Divisor_126_95_q, Divisor_94_63_q_2[31]}),
    .clk(button_3_out), .clr(button_2_out));
  Counter Limit (.load(1'b1), .count(1'b1), .Q(Limit_q), .clk(button_3_out), .clr(button_2_out));  // open: D, carry
  assign PbA = decoder_2_out0 ? R0 : 16'bz;  // Controlled_Buffer controlled_buffer_1
  Register #(.width(16)) u_R0 (.D(Db), .en(decoder_1_out0), .Q(R0), .clk(CCLK), .clr(CRST));
  assign PbB = decoder_3_out0 ? R0 : 16'bz;  // Controlled_Buffer controlled_buffer_2
  assign PbA = decoder_2_out1 ? R1 : 16'bz;  // Controlled_Buffer controlled_buffer_3
  Register #(.width(16)) u_R1 (.D(Db), .en(decoder_1_out1), .Q(R1), .clk(CCLK), .clr(CRST));
  assign PbB = decoder_3_out1 ? R1 : 16'bz;  // Controlled_Buffer controlled_buffer_4
  assign PbA = decoder_2_out2 ? R2 : 16'bz;  // Controlled_Buffer controlled_buffer_5
  Register #(.width(16)) u_R2 (.D(Db), .en(decoder_1_out2), .Q(R2), .clk(CCLK), .clr(CRST));
  assign PbB = decoder_3_out2 ? R2 : 16'bz;  // Controlled_Buffer controlled_buffer_6
  assign PbA = decoder_2_out3 ? R3 : 16'bz;  // Controlled_Buffer controlled_buffer_7
  Register #(.width(16)) u_R3 (.D(Db), .en(decoder_1_out3), .Q(R3), .clk(CCLK), .clr(CRST));
  assign PbB = decoder_3_out3 ? R3 : 16'bz;  // Controlled_Buffer controlled_buffer_8
  assign PbA = decoder_2_out4 ? ST : 16'bz;  // Controlled_Buffer controlled_buffer_9
  Register #(.width(16)) u_ST (.D(Db), .en(decoder_1_out4), .Q(ST), .clk(CCLK), .clr(CRST));
  assign PbB = decoder_3_out4 ? ST : 16'bz;  // Controlled_Buffer controlled_buffer_10
  assign PbA = decoder_2_out5 ? {Flag_SCout, Flag_Cout, Flag_Zero, PF, INT_prog, INT_soft, IRQ_Enable, NMI_Enable} : 16'bz;  // Controlled_Buffer controlled_buffer_11
  assign PbB = decoder_3_out5 ? {Flag_SCout, Flag_Cout, Flag_Zero, PF, INT_prog, INT_soft, IRQ_Enable, NMI_Enable} : 16'bz;  // Controlled_Buffer controlled_buffer_12
  assign PbA = decoder_2_out6 ? PC : 16'bz;  // Controlled_Buffer controlled_buffer_13
  Counter #(.width(16), .max('hffff)) u_PC (
    .load(decoder_1_out6), .D(Db), .count(INC), .Q(PC), .clk(CCLK), .clr(CRST));  // open: carry
  assign PbB = decoder_3_out6 ? PC : 16'bz;  // Controlled_Buffer controlled_buffer_14
  assign PbA = decoder_2_out7 ? imm0 : 16'bz;  // Controlled_Buffer controlled_buffer_15
  Register #(.width(16)) u_imm0 (.D(Db), .en(Si0), .Q(imm0), .clk(CCLK), .clr(CRST));
  assign PbB = and_5_out ? imm0 : 16'bz;  // Controlled_Buffer controlled_buffer_16
  assign PbB = and_4_p1 ? imm1 : 16'bz;  // Controlled_Buffer controlled_buffer_17
  Register #(.width(16)) u_imm1 (.D(Db), .en(Si1), .Q(imm1), .clk(CCLK), .clr(CRST));
  // AND_Gate and_4: pin names not known; wires that end beside it: and_4_p1, and_4_p2
  Decoder #(.select(3), .disabled(0)) decoder_2 (
    .out0(decoder_2_out0), .out1(decoder_2_out1), .out2(decoder_2_out2), .out3(decoder_2_out3),
    .out4(decoder_2_out4), .out5(decoder_2_out5), .out6(decoder_2_out6), .out7(decoder_2_out7), .sel(A),
    .en(and_5_out));
  and and_5 (and_5_out, IA[0], IA[1], IA[2], ~IY, Addr);  // AND_Gate
  ROM #(.addrWidth(16), .dataWidth(16)) rom_1 (.addr(Ab), .data(rom_1_data), .sel(1'b1));
  assign Db = and_6_out ? rom_1_data : 16'bz;  // Controlled_Buffer controlled_buffer_18
  assign controlled_buffer_19_out = WM ? Db : 16'bz;  // Controlled_Buffer controlled_buffer_19
  RAM #(.addrWidth(16), .dataWidth(16)) ram_1 (
    .addr(Ab), .data(controlled_buffer_19_out), .sel(1'b1), .clk(and_3_out), .ld(and_7_p3), .clr(RRST));
  assign Db = and_7_p3 ? controlled_buffer_19_out : 16'bz;  // Controlled_Buffer controlled_buffer_20
  and and_6 (and_6_out, and_8_p3, comparator_1_lt, and_8_p3);
  // AND_Gate and_7: pin names not known; wires that end beside it: comparator_1_lt, RM, and_7_p3
  // AND_Gate and_8: pin names not known; wires that end beside it: comparator_2_gt, comparator_1_lt, and_8_p3, RM
  and and_9 (and_9_out[0], not_2_out, 1'b1);
  not not_2 (not_2_out, multiplexer_3_out);
  Multiplexer #(.width(32)) multiplexer_1 (
    .in0(adder_1_out), .in1(Remainder_31_0_q), .out(multiplexer_1_out), .sel(multiplexer_3_out));  // open: en
  Multiplexer #(.width(32)) multiplexer_2 (
    .in0(adder_2_out), .in1(Remainder_63_32_q), .out(multiplexer_2_out), .sel(multiplexer_3_out));  // open: en
  Adder #(.width(32)) adder_1 (
    .a(Remainder_31_0_q), .b(multiplexer_4_out), .out(adder_1_out), .cout(adder_1_cout));  // open: cin
  Adder #(.width(32)) adder_2 (
    .a(Remainder_63_32_q), .b(multiplexer_5_out), .out(adder_2_out), .cin(adder_1_cout), .cout(adder_2_cout));
  assign not_3_out = ~{Divisor_31_0_q_2[30:0], Divisor_31_0_q[0]};  // NOT_Gate not_3, 32 bits wide
  Adder #(.width(32)) adder_3 (
    .a(not_3_out), .b(pull_resistor_5_node), .out(adder_3_out), .cin(1'b1), .cout(adder_3_cout));
  Pull_Resistor pull_resistor_5 (.node(pull_resistor_5_node));
  not not_4 (not_4_out, 1'b1);
  assign not_5_out = ~{Divisor_94_63_q, Divisor_31_0_q_2[31]};  // NOT_Gate not_5, 32 bits wide
  Adder #(.width(32)) adder_4 (
    .a(not_5_out), .b(pull_resistor_6_node), .out(adder_4_out), .cin(adder_3_cout));  // open: cout
  Pull_Resistor pull_resistor_6 (.node(pull_resistor_6_node));
  Pull_Resistor pull_resistor_7 (.node(pull_resistor_7_node));
  Comparator #(.width(32), .mode("unsigned")) comparator_3 (
    .a(pull_resistor_7_node), .b({Divisor_94_63_q_2[30:0], Divisor_94_63_q[30]}), .eq(comparator_3_eq));  // open: gt, lt
  Pull_Resistor pull_resistor_8 (.node(pull_resistor_8_node));
  Comparator #(.width(32), .mode("unsigned")) comparator_4 (
    .a(pull_resistor_8_node), .b({Divisor_126_95_q, Divisor_94_63_q_2[31]}), .eq(comparator_4_eq));  // open: gt, lt
  Pull_Resistor pull_resistor_9 (.node(pull_resistor_9_node));
  Comparator #(.mode("unsigned")) comparator_5 (
    .a(pull_resistor_9_node), .b(Limit_q), .eq(comparator_5_eq));  // open: gt, lt
  Decoder #(.select(3), .disabled(0)) decoder_3 (
    .out0(decoder_3_out0), .out1(decoder_3_out1), .out2(decoder_3_out2), .out3(decoder_3_out3),
    .out4(decoder_3_out4), .out5(decoder_3_out5), .out6(decoder_3_out6), .out7(and_4_p2), .sel(B));  // open: en
  Multiplexer multiplexer_3 (.in0(or_2_p1), .in1(not_8_out), .out(multiplexer_3_out), .sel(not_4_out));
  Multiplexer #(.width(32)) multiplexer_4 (
    .in0({Accumulator_31_0_q[0], and_9_out[31:1]}), .in1(adder_3_out), .out(multiplexer_4_out), .sel(1'b1));
  Multiplexer #(.width(32)) multiplexer_5 (
    .in0({Accumulator_63_32_q[31], Accumulator_31_0_q[31:1]}), .in1(adder_4_out), .out(multiplexer_5_out),
    .sel(1'b1));  // open: en
  // AND_Gate and_10: pin names not known; wires that end beside it: comparator_3_eq, comparator_4_eq, and_10_p3
  not not_6 (not_6_out, and_10_p3);
  // AND_Gate and_11: pin names not known; wires that end beside it: comparator_4_eq, 1'b1, and_10_p3, and_11_p4
  // OR_Gate or_1: pin names not known; wires that end beside it: and_10_p3, and_11_p4, comparator_5_eq, or_1_p4
  DotMatrix #(.matrixcols(32), .matrixrows(16)) dotmatrix_15 (
    .col0(n32x16_screen_controller_1_col_0), .col1(n32x16_screen_controller_1_col_1),
    .col2(n32x16_screen_controller_1_col_2), .col3(n32x16_screen_controller_1_col_3),
    .col4(n32x16_screen_controller_1_col_4), .col5(n32x16_screen_controller_1_col_5),
    .col6(n32x16_screen_controller_1_col_6), .col7(n32x16_screen_controller_1_col_7),
    .col8(n32x16_screen_controller_1_col_8), .col9(n32x16_screen_controller_1_col_9),
    .col10(n32x16_screen_controller_1_col_10), .col11(n32x16_screen_controller_1_col_11),
    .col12(n32x16_screen_controller_1_col_12), .col13(n32x16_screen_controller_1_col_13),
    .col14(n32x16_screen_controller_1_col_14), .col15(n32x16_screen_controller_1_col_15),
    .col16(n32x16_screen_controller_1_col_16), .col17(n32x16_screen_controller_1_col_17),
    .col18(n32x16_screen_controller_1_col_18), .col19(n32x16_screen_controller_1_col_19),
    .col20(n32x16_screen_controller_1_col_20), .col21(n32x16_screen_controller_1_col_21),
    .col22(n32x16_screen_controller_1_col_22), .col23(n32x16_screen_controller_1_col_23),
    .col24(n32x16_screen_controller_1_col_24), .col25(n32x16_screen_controller_1_col_25),
    .col26(n32x16_screen_controller_1_col_26), .col27(n32x16_screen_controller_1_col_27),
    .col28(n32x16_screen_controller_1_col_28), .col29(n32x16_screen_controller_1_col_29),
    .col30(n32x16_screen_controller_1_col_30), .col31(n32x16_screen_controller_1_col_31));
  _32x16_screen_controller u_32x16_screen_controller_1 (
    .CLOCK(CCLK), .RESET(MRST), .Enable(WM), .Data(Db), .Adress(Ab),
    .Col_0(n32x16_screen_controller_1_col_0), .Col_1(n32x16_screen_controller_1_col_1),
    .Col_2(n32x16_screen_controller_1_col_2), .Col_3(n32x16_screen_controller_1_col_3),
    .Col_4(n32x16_screen_controller_1_col_4), .Col_5(n32x16_screen_controller_1_col_5),
    .Col_6(n32x16_screen_controller_1_col_6), .Col_7(n32x16_screen_controller_1_col_7),
    .Col_8(n32x16_screen_controller_1_col_8), .Col_9(n32x16_screen_controller_1_col_9),
    .Col_10(n32x16_screen_controller_1_col_10), .Col_11(n32x16_screen_controller_1_col_11),
    .Col_12(n32x16_screen_controller_1_col_12), .Col_13(n32x16_screen_controller_1_col_13),
    .Col_14(n32x16_screen_controller_1_col_14), .Col_15(n32x16_screen_controller_1_col_15),
    .Col_16(n32x16_screen_controller_1_col_16), .Col_17(n32x16_screen_controller_1_col_17),
    .Col_18(n32x16_screen_controller_1_col_18), .Col_19(n32x16_screen_controller_1_col_19),
    .Col_20(n32x16_screen_controller_1_col_20), .Col_21(n32x16_screen_controller_1_col_21),
    .Col_22(n32x16_screen_controller_1_col_22), .Col_23(n32x16_screen_controller_1_col_23),
    .Col_24(n32x16_screen_controller_1_col_24), .Col_25(n32x16_screen_controller_1_col_25),
    .Col_26(n32x16_screen_controller_1_col_26), .Col_27(n32x16_screen_controller_1_col_27),
    .Col_28(n32x16_screen_controller_1_col_28), .Col_29(n32x16_screen_controller_1_col_29),
    .Col_30(n32x16_screen_controller_1_col_30), .Col_31(n32x16_screen_controller_1_col_31));
  Comparator #(.width(16), .mode("unsigned")) comparator_6 (
    .a(Ab), .b(16'hfffd), .gt(comparator_6_gt), .eq(comparator_6_eq), .lt(comparator_6_lt));
  not not_7 (not_7_out, adder_2_cout);
  // OR_Gate or_2: pin names not known; wires that end beside it: or_2_p1, not_7_out, not_6_out
  not not_8 (not_8_out, Divisor_94_63_q[30]);
  assign controlled_buffer_21_out = not_9_out ? PbA : 16'bz;  // Controlled_Buffer controlled_buffer_21
  assign controlled_buffer_22_out = not_10_out ? PbB : 16'bz;  // Controlled_Buffer controlled_buffer_22
  not not_9 (not_9_out, AXA);
  not not_10 (not_10_out, AXB);
  Pull_Resistor pull_resistor_10 (.node(Rb));
  Register #(.width(16)) u_AR (.D(Rb), .en(SAr), .Q(AR), .clk(CCLK), .clr(CRST));
  Button button_4 (.out(button_4_out));
  Button button_5 (.out(button_5_out));
  Button button_6 (.out(button_6_out));
  Button v (.out(v_out));
  Button_inputs button_inputs_1 (
    .Left(button_5_out), .Up(button_4_out), .Down(v_out), .Right(button_6_out), .Start(Sta_out),
    .Select(Sel_out), .X(X_out), .A(A_out), .Y(Y_out), .B(B_out), .Clock(CCLK), .Reset(MRST),
    .Data_out(button_inputs_1_data_out));  // open: Clear_interrupt, Interrupt
  // AND_Gate and_12: pin names not known; wires that end beside it: comparator_6_gt, comparator_6_eq, comparator_6_lt, RM, and_12_p5
  assign Db = and_12_p5 ? button_inputs_1_data_out : 16'bz;  // Controlled_Buffer controlled_buffer_23
  assign controlled_buffer_21_out = AXA ? {16{1'b0}} : 16'bz;  // Controlled_Buffer controlled_buffer_24
  assign controlled_buffer_22_out = AXB ? {16{1'b0}} : 16'bz;  // Controlled_Buffer controlled_buffer_25
  not not_11 (not_11_out, RbC);
  Multiplexer #(.width(16)) multiplexer_6 (.in0(Rb), .in1(AR), .out(Ab), .sel(WM));  // open: en
  not not_12 (not_12_out, RM);
  Button X (.out(X_out));
  Button Sel (.out(Sel_out));
  Button Sta (.out(Sta_out));
  ExactlyOne xor_1[15:0] (
    .out(xor_1_out), .in1(controlled_buffer_21_out), .in3(bit_extender_2_out), .in4(controlled_buffer_22_out));
  ExactlyOne xor_2[15:0] (
    .out(xor_2_out), .in0(bit_extender_2_out), .in1(controlled_buffer_22_out), .in3(bit_extender_1_out));
  assign bit_extender_1_out = {{15{AIB}}, AIB};  // Bit_Extender bit_extender_1
  assign bit_extender_2_out = {{15{AIA}}, AIA};  // Bit_Extender bit_extender_2
  assign bit_extender_3_out = {{15{AIA}}, AIA};  // Bit_Extender bit_extender_3
  Comparator #(.width(16), .mode("unsigned")) comparator_7 (
    .a({16{1'b0}}), .b(controlled_buffer_28_out), .eq(Zero));  // open: gt, lt
  assign Rb = not_11_out ? controlled_buffer_28_out : 16'bz;  // Controlled_Buffer controlled_buffer_26
  assign Db = not_12_out ? Rb : 16'bz;  // Controlled_Buffer controlled_buffer_27
  Button Y (.out(Y_out));
  Button u_B (.out(B_out));
  Button u_A (.out(A_out));
  ExactlyOne xor_3[15:0] (.out(xor_3_out), .in1(xor_1_out), .in3(16'h8000), .in4(xor_2_out));
  ExactlyOne xor_4[15:0] (.out(xor_4_out), .in0(16'h8000), .in1(xor_2_out), .in3(16'h8000));
  // OR_Gate #(.width(16)) or_3: pin names not known; wires that end beside it: xor_1_out, xor_2_out, or_3_p3
  Pull_Resistor pull_resistor_11 (.node({pull_resistor_11_node[15:4], Intr_3, pull_resistor_11_node[2:0]}));
  Pull_Resistor pull_resistor_12 (.node({SCout, Cout, Zero, pull_resistor_12_node, INT_prog, INT_soft, IRQ_Enable, NMI_Enable}));
  Multiplexer #(.width(16)) multiplexer_7 (
    .in0({SCout, Cout, Zero, pull_resistor_12_node, INT_prog, INT_soft, IRQ_Enable, NMI_Enable}), .in1(Db),
    .out(multiplexer_7_out), .sel(WPF));  // open: en
  assign controlled_buffer_28_out = AADD ? adder_5_out : 16'bz;  // Controlled_Buffer controlled_buffer_28
  Adder #(.width(16)) adder_5 (.a(xor_1_out), .b(xor_2_out), .out(adder_5_out), .cin(Cin), .cout(adder_5_cout));
  assign Cout = AADD ? adder_5_cout : 1'bz;  // Controlled_Buffer controlled_buffer_29
  Adder #(.width(16)) adder_6 (.a(xor_3_out), .b(xor_4_out), .cin(Cin), .cout(SCout));  // open: out
  Pull_Resistor pull_resistor_13 (.node(Cout));
  assign xor_5_out = xor_1_out ^ xor_2_out;  // XOR_Gate xor_5, 16 bits wide
  assign controlled_buffer_28_out = AXOR ? xor_5_out : 16'bz;  // Controlled_Buffer controlled_buffer_30
  assign controlled_buffer_28_out = AOR ? xor_6_out : 16'bz;  // Controlled_Buffer controlled_buffer_31
  assign xor_6_out = or_3_p3 ^ bit_extender_3_out;  // XOR_Gate xor_6, 16 bits wide
  assign controlled_buffer_28_out = ASHL ? {xor_1_out[14:0], Cin} : 16'bz;  // Controlled_Buffer controlled_buffer_32
  assign Cout = ASHL ? xor_1_out[15] : 1'bz;  // Controlled_Buffer controlled_buffer_33
  assign controlled_buffer_28_out = ASHR ? {Cin, xor_1_out[15:1]} : 16'bz;  // Controlled_Buffer controlled_buffer_34
  assign Cout = ASHR ? xor_1_out[0] : 1'bz;  // Controlled_Buffer controlled_buffer_35
  assign bit_extender_4_out = {{15{xor_2_out[15]}}, xor_2_out[15]};  // Bit_Extender bit_extender_4
  assign controlled_buffer_28_out = CX ? bit_extender_4_out : 16'bz;  // Controlled_Buffer controlled_buffer_36
  assign or_4_out = {pull_resistor_11_node[15:4], Intr_3, pull_resistor_11_node[2:0]} | multiplexer_7_out;  // OR_Gate or_4, 16 bits wide
  Register #(.width(16)) u_PF (
    .D(or_4_out), .en(or_5_out),
    .Q({Flag_SCout, Flag_Cout, Flag_Zero, PF, INT_prog, INT_soft, IRQ_Enable, NMI_Enable}), .clk(CCLK),
    .clr(CRST));
  or or_5 (or_5_out, WPF, Intr_3, Act);
  Pull_Resistor pull_resistor_14 (.node(Db));
  Comparator #(.width(16), .mode("unsigned")) comparator_8 (
    .a(Ab), .b(16'hfff6), .gt(comparator_8_gt), .eq(comparator_8_eq), .lt(comparator_8_lt));
  Comparator #(.width(16), .mode("unsigned")) comparator_9 (
    .a(Ab), .b(16'hfff5), .gt(comparator_9_gt), .eq(comparator_9_eq), .lt(comparator_9_lt));
  Comparator #(.width(16), .mode("unsigned")) comparator_10 (
    .a(Ab), .b({16{1'b1}}), .gt(comparator_10_gt), .eq(comparator_10_eq), .lt(comparator_10_lt));
  TTY #(.rows(11), .cols(40)) tty_1 (.data(Db[6:0]), .clk(CCLK), .we(and_13_p6), .clr(MRST));
  // AND_Gate and_13: pin names not known; wires that end beside it: comparator_8_gt, comparator_8_eq, comparator_8_lt, WM, comparator_9_eq, and_13_p6
  // AND_Gate and_14: pin names not known; wires that end beside it: comparator_9_gt, comparator_9_eq, comparator_9_lt, WM, RM, and_14_p6
  // AND_Gate and_15: pin names not known; wires that end beside it: comparator_10_gt, comparator_10_eq, comparator_10_lt, RM, and_15_p5
  assign Db = and_15_p5 ? 16'h40 : 16'bz;  // Controlled_Buffer controlled_buffer_37
  and and_16 (and_16_out, Addr, nand_1_p4);
  // NAND_Gate nand_1: pin names not known; wires that end beside it: IX[0], nand_1_p2, IX[2], nand_1_p4
  or or_6 (or_6_out, Boot_0, Boot_1, Pop);
  or or_7 (or_7_out, Push, Intr_0, Intr_2);
  or or_8 (or_8_out, or_7_out, or_6_out);
  Keyboard #(.buflen(40)) keyboard_1 (.clk(CCLK), .re(and_14_p6), .clr(MRST), .data(keyboard_1_data));  // open: avail
  assign Db[6:0] = and_14_p6 ? keyboard_1_data : 7'bz;  // Controlled_Buffer controlled_buffer_38
  Decoder #(.select(3), .disabled(0), .enable("true")) decoder_4 (
    .out0(decoder_4_out0), .out1(decoder_4_out1), .out2(CMP), .out3(AIA), .out4(decoder_4_out4), .out5(AXOR),
    .out6(ASHL), .out7(ASHR), .sel(IOp[2:0]), .en(Act));
  or or_9 (or_9_out, and_16_out, or_6_out, decoder_4_out0);
  // AND_Gate and_17: pin names not known; wires that end beside it: IOp[4], Act, and_17_p3
  or or_10 (AXB, and_17_p3, or_8_out, or_8_out);
  or or_11 (or_11_out, or_8_out, or_8_out, Act);
  and and_18 (and_18_out, ~multiplexer_8_out[0], ~multiplexer_8_out[1], multiplexer_8_out[2]);  // AND_Gate
  Multiplexer #(.width(3)) multiplexer_8 (
    .in0(Db[11:9]), .in1(3'b111), .out(multiplexer_8_out), .sel(not_13_out));  // open: en
  // OR_Gate or_12: pin names not known; wires that end beside it: or_12_p1, or_12_p2, Load_0
  Multiplexer #(.width(3)) multiplexer_9 (
    .in0(Db[8:6]), .in1(3'b111), .out(multiplexer_9_out), .sel(not_13_out));  // open: en
  // OR_Gate or_13: pin names not known; wires that end beside it: or_13_p1, or_13_p2, Load_0
  not not_13 (not_13_out, Load_0);
  Demultiplexer #(.disabled(0)) demultiplexer_1 (.out0(or_13_p1), .out1(or_12_p1), .in(Addr), .sel(IY));
  nor nor_1 (AXA, Act, or_7_out, or_9_out);
  or or_14 (or_14_out, decoder_4_out1, or_7_out, CMP);
  not not_14 (not_14_out, or_9_out);
  // AND_Gate and_19: pin names not known; wires that end beside it: or_8_out, IOp[3], and_19_p3
  Register #(.width(1)) Y_2 (.D(Db[15]), .en(Load_0), .Q(IY), .clk(CCLK), .clr(CRST));
  Register #(.width(3)) X_2 (.D(Db[14:12]), .en(Load_0), .Q(IX), .clk(CCLK), .clr(CRST));
  Register #(.width(3)) B_2 (.D(multiplexer_8_out), .en(or_12_p2), .Q(IB), .clk(CCLK), .clr(CRST));
  Register #(.width(3)) A_2 (.D(multiplexer_9_out), .en(or_13_p2), .Q(IA), .clk(CCLK), .clr(CRST));
  Register #(.width(6)) Opcode (.D(Db[5:0]), .en(Load_0), .Q(IOp), .clk(CCLK), .clr(CRST));
  Register #(.width(1)) u_Is_ST (.D(and_18_out), .en(Load_0), .Q(Is_ST), .clk(CCLK), .clr(CRST));
  or or_15 (or_15_out, AXA, or_9_out, or_14_out);
  // OR_Gate or_16: pin names not known; wires that end beside it: or_14_out, AIA, AIB
  // OR_Gate or_17: pin names not known; wires that end beside it: or_14_out, AIA, decoder_4_out4, AOR
  // XOR_Gate xor_7: pin names not known; wires that end beside it: not_14_out, AXB, Flag_Cout, xor_7_p4
  Multiplexer #(.disabled(0), .enable("true")) multiplexer_10 (
    .in0(xor_7_p4), .in1(Flag_Cout), .out(Cin), .sel(and_19_p3), .en(or_11_out));
  Register #(.width(16), .trigger("falling")) PS (
    .D({Intr_3, Intr_2, Intr_1, Intr_0, demultiplexer_8_out0, Boot_0, 1'b1}),
    .Q({Intr_4, Intr_3, Intr_2, Intr_1, Intr_0, Pop, Mov, Act, Addr, Jsr, Push, Load_2, Load_1, Load_0, Boot_1, PS_q[0]}),
    .clk(CCLK), .clr(CRST));  // open: en
  Comparator #(.width(16), .mode("unsigned")) comparator_11 (
    .a(Ab), .b(16'hfffe), .eq(comparator_11_eq));  // open: gt, lt
  and and_20 (and_20_out, comparator_11_eq, RM);
  Comparator #(.width(16), .mode("unsigned")) comparator_12 (
    .a(Ab), .b(16'hfffb), .eq(comparator_12_eq));  // open: gt, lt
  Comparator #(.width(16), .mode("unsigned")) comparator_13 (
    .a(Ab), .b(16'hfffa), .eq(comparator_13_eq));  // open: gt, lt
  Comparator #(.width(16), .mode("unsigned")) comparator_14 (
    .a(Ab), .b(16'hfff9), .eq(comparator_14_eq));  // open: gt, lt
  Comparator #(.width(16), .mode("unsigned")) comparator_15 (
    .a(Ab), .b(16'hfff8), .eq(comparator_15_eq));  // open: gt, lt
  and and_21 (and_21_out, WM, CCLK);
  and and_22 (CX, Mov, Is_CX);
  not not_15 (Boot_0, PS_q[0]);
  and and_23 (and_23_out, ~IA[0], ~IA[1], IA[2]);  // AND_Gate
  Multiplexer #(.disabled(0), .enable("true")) multiplexer_11 (
    .in0(and_23_out), .in1(Is_ST), .out(multiplexer_11_out), .sel(IY), .en(nand_2_out));
  nand nand_2 (nand_2_out, IX[0], IX[1], IX[2]);
  assign Db[7:0] = and_20_out ? {Mode_q[7], No_Timer_Wake, No_Button_Wake, Screen_Disable, Mode_q[3], Timer_IRQ, Timer_NMI, Timer_Enable} : 8'bz;  // Controlled_Buffer controlled_buffer_39
  and and_24 (and_24_out, RM, comparator_13_eq);
  assign Db = and_24_out ? Temp_Low_q : 16'bz;  // Controlled_Buffer controlled_buffer_40
  assign Db = and_25_out ? Limit_Low_q : 16'bz;  // Controlled_Buffer controlled_buffer_41
  and and_25 (and_25_out, RM, comparator_15_eq);
  // AND_Gate and_26: pin names not known; wires that end beside it: CX, or_15_out, AADD
  or or_18 (or_18_out, Intr_4, Boot_1, Pop);
  Demultiplexer #(.disabled(0)) demultiplexer_2 (
    .out0(demultiplexer_2_out0), .out1(demultiplexer_8_out0[10]), .in(or_19_out), .sel(demultiplexer_3_out1));  // open: en
  or or_19 (or_19_out, Intr_4, Act, Mov);
  Demultiplexer #(.disabled(0)) demultiplexer_3 (
    .out0(demultiplexer_3_out0), .out1(demultiplexer_3_out1), .in(multiplexer_11_out), .sel(IY));
  Register Mode (
    .D(Db[7:0]), .en(comparator_11_eq),
    .Q({Mode_q[7], No_Timer_Wake, No_Button_Wake, Screen_Disable, Mode_q[3], Timer_IRQ, Timer_NMI, Timer_Enable}),
    .clk(and_21_out), .clr(MRST));
  assign {controlled_buffer_42_out[7], Sleep_Deep, Sleep_Light, Sleep_Idle, Button_Ack, Timer_Ack, Timer_Read, Timer_Write} = comparator_11_eq ? Db[15:8] : 8'bz;  // Controlled_Buffer controlled_buffer_42
  Pull_Resistor pull_resistor_15 (.node({controlled_buffer_42_out[7], Sleep_Deep, Sleep_Light, Sleep_Idle, Button_Ack, Timer_Ack, Timer_Read, Timer_Write}));
  or or_20 (or_20_out, comparator_13_eq, Timer_Read);
  Multiplexer #(.width(16)) multiplexer_12 (.in0(Db), .in1(Timer_q), .out(multiplexer_12_out), .sel(Timer_Read));
  Register #(.width(16)) Temp_Low (
    .D(multiplexer_12_out), .en(or_20_out), .Q(Temp_Low_q), .clk(and_21_out), .clr(MRST));
  Register #(.width(16)) Limit_Low (.D(Db), .en(comparator_15_eq), .Q(Limit_Low_q), .clk(and_21_out), .clr(MRST));
  or or_21 (or_21_out, demultiplexer_5_out1, or_18_out, demultiplexer_2_out0);
  Demultiplexer #(.disabled(0)) demultiplexer_4 (
    .out0(demultiplexer_8_out0[3]), .out1(demultiplexer_4_out1), .in(Load_0), .sel(nand_3_out));
  Demultiplexer #(.disabled(0)) demultiplexer_5 (
    .out0(demultiplexer_5_out0), .out1(demultiplexer_5_out1), .in(Addr), .sel(Is_LEA));  // open: en
  nand nand_3 (nand_3_out, IA[0], IA[1], IA[2]);
  nand nand_4 (nand_4_out, IB[0], IB[1], IB[2]);
  Multiplexer #(.width(16)) multiplexer_13 (.in0(Db), .in1(Timer_q_2), .out(multiplexer_13_out), .sel(Timer_Read));
  and and_27 (and_27_out, RM, comparator_12_eq);
  assign Db = and_27_out ? Temp_High_q : 16'bz;  // Controlled_Buffer controlled_buffer_43
  assign Db = and_28_out ? Limit_High_q : 16'bz;  // Controlled_Buffer controlled_buffer_44
  and and_28 (and_28_out, RM, comparator_14_eq);
  or or_22 (or_22_out[2], R6, R4);
  Multiplexer #(.width(3), .disabled(0)) multiplexer_14 (
    .in0(IA), .in1(IB), .out(multiplexer_14_out), .sel(IY));  // open: en
  or or_23 (WM, WR7, Jsr, Intr_1, Intr_3);
  // OR_Gate or_24: pin names not known; wires that end beside it: demultiplexer_4_out1, Load_1, or_24_p3
  Demultiplexer #(.disabled(0)) demultiplexer_6 (
    .out0(demultiplexer_8_out0[4]), .out1(demultiplexer_6_out1), .in(or_24_p3), .sel(nand_4_out));
  Demultiplexer #(.disabled(0)) demultiplexer_7 (
    .out0(demultiplexer_8_out0[5]), .out1(demultiplexer_7_out1), .in(or_25_p3), .sel(nor_2_p2));  // open: en
  // OR_Gate or_25: pin names not known; wires that end beside it: demultiplexer_6_out1, Load_2, or_25_p3
  // NOR_Gate nor_2: pin names not known; wires that end beside it: demultiplexer_3_out0, nor_2_p2, Is_JSR
  not not_16 (not_16_out, nand_2_out);
  or or_26 (or_26_out, comparator_12_eq, Timer_Read);
  Register #(.width(16)) Temp_High (
    .D(multiplexer_13_out), .en(or_26_out), .Q(Temp_High_q), .clk(and_21_out), .clr(MRST));
  Register #(.width(16)) Limit_High (.D(Db), .en(comparator_14_eq), .Q(Limit_High_q), .clk(and_21_out), .clr(MRST));
  Multiplexer #(.width(3), .disabled(0)) multiplexer_15 (
    .in0(multiplexer_14_out), .in1(IB), .out(multiplexer_15_out), .sel(Mov));  // open: en
  Demultiplexer #(.disabled(0)) demultiplexer_8 (
    .out0(demultiplexer_8_out0[2]), .out1(demultiplexer_8_out0[11]), .in(or_21_out), .sel(Is_INTR));  // open: en
  Demultiplexer #(.disabled(0)) demultiplexer_9 (
    .out0(demultiplexer_8_out0[6]), .out1(demultiplexer_9_out1), .in(Push), .sel(not_18_out));  // open: en
  or or_27 (or_27_out, Jsr, Jsr, demultiplexer_7_out1);
  Demultiplexer #(.disabled(0)) demultiplexer_10 (
    .out0(demultiplexer_10_out0), .out1(demultiplexer_10_out1), .in(or_27_out), .sel(not_16_out));  // open: en
  or or_28 (or_28_out, INT_prog, register_1_q);
  Register #(.width(1)) register_1 (.D(INT_prog), .en(Load_0), .Q(register_1_q), .clk(CCLK), .clr(CRST));
  not not_17 (not_17_out, Timer_Write);
  Counter #(.width(32), .max('hffffffff)) Timer (
    .load(Timer_Write), .D({Temp_High_q, Temp_Low_q}), .count(not_17_out), .Q({Timer_q_2, Timer_q}),
    .clk(TCLK), .clr(MRST));  // open: carry
  assign A = or_22_out[2] ? {or_22_out[2], R6, Intr_3} : 3'bz;  // Controlled_Buffer controlled_buffer_45
  assign A = Addr ? IX : 3'bz;  // Controlled_Buffer controlled_buffer_46
  Pull_Resistor pull_resistor_16 (.node(A));
  assign A = Rp ? IA : 3'bz;  // Controlled_Buffer controlled_buffer_47
  assign B = or_22_out[2] ? {or_22_out[2], R6, Intr_3} : 3'bz;  // Controlled_Buffer controlled_buffer_48
  assign B = Addr ? multiplexer_15_out : 3'bz;  // Controlled_Buffer controlled_buffer_49
  Pull_Resistor pull_resistor_17 (.node(B));
  assign B = Rp ? IB : 3'bz;  // Controlled_Buffer controlled_buffer_50
  assign D = or_22_out[2] ? {or_22_out[2], R6, Intr_3} : 3'bz;  // Controlled_Buffer controlled_buffer_51
  assign D = Addr ? IA : 3'bz;  // Controlled_Buffer controlled_buffer_52
  Pull_Resistor pull_resistor_18 (.node(D));
  assign D = Rp ? IA : 3'bz;  // Controlled_Buffer controlled_buffer_53
  or or_29 (demultiplexer_8_out0[7], demultiplexer_9_out1, demultiplexer_10_out0);
  or or_30 (or_30_out, demultiplexer_10_out1, demultiplexer_5_out0);
  Demultiplexer #(.disabled(0)) demultiplexer_11 (
    .out0(demultiplexer_8_out0[8]), .out1(demultiplexer_8_out0[9]), .in(or_30_out), .sel(IOp[5]));  // open: en
  not not_18 (not_18_out, Is_JSR);
  // AND_Gate and_29: pin names not known; wires that end beside it: IOp[4], IOp[5], Is_LEA
  // AND_Gate #(.out("Z1")) and_30: pin names not known; wires that end beside it: and_30_p1, and_30_p2, No_Timer_Wake, Wake
  // AND_Gate #(.out("Z1")) and_31: pin names not known; wires that end beside it: and_30_p1, and_30_p2, and_30_p2, No_Timer_Wake, NMI
  and and_32 (IRQ, Timer_NMI, and_30_p2, Timer_IRQ);
  Comparator #(.width(32), .mode("unsigned")) comparator_16 (
    .a({Timer_q_2, Timer_q}), .b({Limit_High_q, Limit_Low_q}), .eq(comparator_16_eq));  // open: gt, lt
  and and_33 (TCLK, MCLK, or_31_out);
  or or_31 (or_31_out, Timer_Write, Timer_Enable);
  and and_34 (and_34_out, IRQ, IRQ_Enable, and_35_p1);
  // OR_Gate or_32: pin names not known; wires that end beside it: and_34_out, or_32_p2, or_32_p3, or_28_out
  // AND_Gate and_35: pin names not known; wires that end beside it: and_35_p1, NMI, NMI_Enable, or_32_p2
  S_R_Flip_Flop s_r_ff_1 (.Q(and_30_p2), .preset(comparator_16_eq), .reset(Timer_Ack));  // open: S, clk, R, Qn, en
  buf and_36 (Is_INTR, ~or_32_p3);  // AND_Gate AND_Gate
  Multiplexer multiplexer_16 (.in0(Flag_Cout), .in1(Flag_SCout), .out(multiplexer_16_out), .sel(IOp[1]));  // open: en
  and and_37 (and_37_out, Addr, Is_LEA);
  // AND_Gate and_38: pin names not known; wires that end beside it: multiplexer_16_out, and_38_p2, multiplexer_16_out, Flag_Zero, Flag_Zero, and_38_p6
  // AND_Gate and_39: pin names not known; wires that end beside it: Flag_Zero, and_38_p2, multiplexer_16_out, multiplexer_16_out, and_39_p5
  nor nor_3 (nor_3_out, IOp[5], and_37_out, Mov);
  or or_33 (or_33_out, Push, Intr_0, Intr_2);
  or or_34 (or_34_out, Jsr, Intr_1);
  // OR_Gate or_35: pin names not known; wires that end beside it: Pop, Addr, or_35_p3, or_33_out
  // AND_Gate and_40: pin names not known; wires that end beside it: Mov, Addr, Is_LEA, and_40_p4
  and and_41 (and_41_out[0], Intr_4, NMI);
  Register #(.width(3)) Sleep (
    .D({Sleep_Deep, Sleep_Light, Sleep_Idle}), .Q(Sleep_q), .clk(and_42_out), .clr(or_36_out));  // open: en
  and and_42 (and_42_out, WM, CCLK);
  or or_36 (or_36_out, MRST, Wake, Wake);
  Pull_Resistor pull_resistor_19 (.node(Wake));
  Multiplexer #(.select(2), .disabled(0)) multiplexer_17 (
    .in0(and_38_p6), .in1(and_39_p5), .in2(Flag_Zero), .in3(multiplexer_16_out), .out(multiplexer_17_out),
    .sel({IOp[2], IOp[0]}));  // open: en
  not not_19 (not_19_out, IOp[3]);
  or or_37 (RbC, 1'b0, Intr_4);
  assign Rb = RbC ? {and_41_out[15:2], 1'b0, and_41_out[0]} : 16'bz;  // Controlled_Buffer controlled_buffer_54
  buf buffer_5 (buffer_5_out, Sleep_q[2]);
  or or_38 (or_38_out, Sleep_q[2], Sleep_q[1]);
  Multiplexer multiplexer_18 (
    .in0(multiplexer_17_out), .in1(not_19_out), .out(multiplexer_18_out), .sel(and_44_p2));  // open: en
  and and_43 (Is_JSR, ~IOp[0], IOp[1], IOp[2], IOp[3], IOp[5]);  // AND_Gate
  // AND_Gate and_44: pin names not known; wires that end beside it: IOp[1], and_44_p2, IOp[2]
  and and_45 (Is_CX, IOp[0], IOp[1], IOp[2], IOp[3], IOp[5]);
  or or_39 (or_39_out, Boot_0, Boot_1, Load_0);
  // OR_Gate or_40: pin names not known; wires that end beside it: Load_1, Load_1, Load_2, INC
  // AND_Gate and_46: pin names not known; wires that end beside it: Is_LEA, Addr, and_46_p3
  nor nor_4 (CPUCE, Sleep_q[0], Sleep_q[1], Sleep_q[2]);
  ExactlyOne xor_8 (.out(xor_8_out), .in1(multiplexer_18_out), .in3(IOp[3]), .in4(IOp[3]));
  or or_41 (Cond_met, xor_8_out, nor_3_out);
  or or_42 (R6, Intr_4, INC, or_39_out, or_34_out);
  or or_43 (or_43_out, or_33_out, Pop);
  or or_44 (or_44_out, INC, Boot_1, and_46_p3);
  Demultiplexer #(.disabled(0), .enable("true")) demultiplexer_12 (
    .out0(demultiplexer_12_out0), .out1(demultiplexer_12_out1), .in(Addr), .sel(IY), .en(not_20_out));
  not not_20 (not_20_out, and_40_p4);
  // AND_Gate and_47: pin names not known; wires that end beside it: CMP, Act, and_47_p3
  // OR_Gate or_45: pin names not known; wires that end beside it: Load_1, demultiplexer_12_out0, Si0
  // OR_Gate or_46: pin names not known; wires that end beside it: Load_2, demultiplexer_12_out1, Si1
  // OR_Gate or_47: pin names not known; wires that end beside it: or_43_out, Intr_3, R4
  // OR_Gate or_48: pin names not known; wires that end beside it: Addr, or_33_out, SAr
  or or_49 (Rp, Mov, Act);
  or or_50 (RM, or_44_out, Intr_4);
  or or_51 (or_51_out, or_39_out, Mov, and_40_p4, or_35_p3, and_47_p3);
  and and_48 (and_48_out, or_51_out, Cond_met, Intr_4);
  or or_52 (WR, and_48_out, Intr_4);

  // Other names for the same wires on the sheet: PF (some bits) = {Flag_SCout, Flag_Cout, Flag_Zero, INT_prog, INT_soft, IRQ_Enable, NMI_Enable};
  //   Ra = Addr; R5 = Intr_3

  // Notes on the sheet:
  //   buffer_1 drives only 1 and floats otherwise
  //   buffer_2 drives only 1 and floats otherwise
  //   buffer_3 drives only 1 and floats otherwise
  //   Memory
  //   Registers file
  //   buffer_4 drives only 1 and floats otherwise
  //   Divide and multiply unit
  //   contents of rom_1 (hex, n*v repeats v):
  //   3 3 3 7f26 ffff df01 ffff 7e26 be 7e66 6c 7ea6 e 7fae 5c 7066 7e41 be 7191 5326 efb6 4 d066 53e6
  //   fff6 7010 5012 efb8 fff9 d866 d9a6 7091 7fad 29 5726 a2e6 2626 7091 7fa5 23 d8e6 d9a6 7092 7fa8 2e
  //   d9a6 7202 7fa0 22 5726 7400 7010 7440 7050 7e85 ffff a2e6 2626 7090 7fad 38 d8e6 d9a6 7091 7fad 46
  //   2226 7091 7fa5 42 d9a6 7092 7fa0 5a 5726 7400 7440 7e85 ffff 7090 a0e6 a2c1 7fac 57 7090 7fad 50
  //   7626 d8e6 d9a6 7005 d9a6 7092 7fa0 6a 7400 7440 7e85 ffff 7090 2202 7fa4 6c 7090 7fad 64 7005 d9a6
  //   a036 d9a6 7091 7fad 77 2202 7fa4 79 7091 7fa5 71 7005 d9a6 a036 d9a6 5526 7201 efb6 3 90a6 5466 7050
  //   1012 efb0 3 5052 efb8 fff7 7200 d8a6 d9a6 5726 7092 efb8 2 d8e6 d9a6 5526 7400 7200 7e85 ffff 7090
  //   a2e6 2626 5326 7066 7fa6 9e 7010 5012 7fa8 9d 7201 d866 d9a6 7fa6 a7 7010 5202 7fa4 ae 5012 7fa8 a6
  //   7005 d9a6 5526 7485 7fa6 b4 7010 5202 7fac b8 70a6 5012 7fa8 b3 7426 d8a6 d9a6 48 65 6c 6c 6f 2c 20
  //   57 6f 72 6c 64 21 0 48 65 6c 6c 6f 2c 20 57 6f 72 6c 64 21 0 68 45 4c 4c 4f 2c 20 77 6f 72 6c 44 21
  //   0 72 6c 44 21
  //   User interface
  //   Arithmetic and Logic Unit
  //   SHL
  //   SHR
  //   Flags register
  //   Crappy UART maybe of
  //   MMIO length
  //   ALU decoder
  //   ADD
  //   SUB
  //   CMP
  //   AND
  //   OR
  //   XOR
  //   SHL
  //   SHR
  //   CC
  //   MATH1
  //   Instruction unpacker
  //   PASS
  //   Timer 0
  //   State machine
  //   Register decoder
  //   and_30 drives only 1 and floats otherwise
  //   and_31 drives only 1 and floats otherwise
  //   and_32 drives only 1 and floats otherwise
  //   Condition decoder
  //   Miscellaneous decoders
  //   LT
  //   GT
  //   EQ
  //   CS
  //   buffer_5 drives only 1 and floats otherwise
endmodule

module _32x16_screen_controller (
  input  CLOCK,
  input  RESET,
  input  Enable,
  input  [15:0] Data,
  input  [15:0] Adress,
  output [15:0] Col_0,
  output [15:0] Col_1,
  output [15:0] Col_2,
  output [15:0] Col_3,
  output [15:0] Col_4,
  output [15:0] Col_5,
  output [15:0] Col_6,
  output [15:0] Col_7,
  output [15:0] Col_8,
  output [15:0] Col_9,
  output [15:0] Col_10,
  output [15:0] Col_11,
  output [15:0] Col_12,
  output [15:0] Col_13,
  output [15:0] Col_14,
  output [15:0] Col_15,
  output [15:0] Col_16,
  output [15:0] Col_17,
  output [15:0] Col_18,
  output [15:0] Col_19,
  output [15:0] Col_20,
  output [15:0] Col_21,
  output [15:0] Col_22,
  output [15:0] Col_23,
  output [15:0] Col_24,
  output [15:0] Col_25,
  output [15:0] Col_26,
  output [15:0] Col_27,
  output [15:0] Col_28,
  output [15:0] Col_29,
  output [15:0] Col_30,
  output [15:0] Col_31
);

  wire and_1_out, and_2_out, comparator_1_lt, decoder_1_out0, decoder_1_out1, decoder_1_out2, decoder_1_out3,
       decoder_1_out4, decoder_1_out5, decoder_1_out6, decoder_1_out7, decoder_1_out8, decoder_1_out9,
       decoder_1_out10, decoder_1_out11, decoder_1_out12, decoder_1_out13, decoder_1_out14, decoder_1_out15,
       decoder_1_out16, decoder_1_out17, decoder_1_out18, decoder_1_out19, decoder_1_out20, decoder_1_out21,
       decoder_1_out22, decoder_1_out23, decoder_1_out24, decoder_1_out25, decoder_1_out26, decoder_1_out27,
       decoder_1_out28, decoder_1_out29, decoder_1_out30, decoder_1_out31, subtractor_1_bout;
  wire [4:0] bit_extender_1_out;
  wire [15:0] subtractor_1_out;

  Subtractor #(.width(16)) subtractor_1 (
    .a(Adress), .b(16'hffc0), .out(subtractor_1_out), .bout(subtractor_1_bout));  // open: bin
  buf and_1 (and_1_out, Enable);  // AND_Gate AND_Gate
  Bit_Extender #(.in_width(16), .out_width(5)) bit_extender_1 (.in(subtractor_1_out), .out(bit_extender_1_out));
  Comparator #(.width(16), .mode("unsigned")) comparator_1 (
    .a(subtractor_1_out), .b(16'h20), .lt(comparator_1_lt));  // open: gt, eq
  Decoder #(.select(5), .disabled(0), .enable("true")) decoder_1 (
    .out0(decoder_1_out0), .out1(decoder_1_out1), .out2(decoder_1_out2), .out3(decoder_1_out3),
    .out4(decoder_1_out4), .out5(decoder_1_out5), .out6(decoder_1_out6), .out7(decoder_1_out7),
    .out8(decoder_1_out8), .out9(decoder_1_out9), .out10(decoder_1_out10), .out11(decoder_1_out11),
    .out12(decoder_1_out12), .out13(decoder_1_out13), .out14(decoder_1_out14), .out15(decoder_1_out15),
    .out16(decoder_1_out16), .out17(decoder_1_out17), .out18(decoder_1_out18), .out19(decoder_1_out19),
    .out20(decoder_1_out20), .out21(decoder_1_out21), .out22(decoder_1_out22), .out23(decoder_1_out23),
    .out24(decoder_1_out24), .out25(decoder_1_out25), .out26(decoder_1_out26), .out27(decoder_1_out27),
    .out28(decoder_1_out28), .out29(decoder_1_out29), .out30(decoder_1_out30), .out31(decoder_1_out31),
    .sel(bit_extender_1_out), .en(and_2_out));
  and and_2 (and_2_out, comparator_1_lt, and_1_out);
  Register #(.width(16)) register_1 (
    .D({Data[0], Data[1], Data[2], Data[3], Data[4], Data[5], Data[6], Data[7], Data[8], Data[9], Data[10], Data[11], Data[12], Data[13], Data[14], Data[15]}),
    .en(decoder_1_out0), .Q(Col_0), .clk(CLOCK), .clr(RESET));
  Register #(.width(16)) register_2 (
    .D({Data[0], Data[1], Data[2], Data[3], Data[4], Data[5], Data[6], Data[7], Data[8], Data[9], Data[10], Data[11], Data[12], Data[13], Data[14], Data[15]}),
    .en(decoder_1_out1), .Q(Col_1), .clk(CLOCK), .clr(RESET));
  Register #(.width(16)) register_3 (
    .D({Data[0], Data[1], Data[2], Data[3], Data[4], Data[5], Data[6], Data[7], Data[8], Data[9], Data[10], Data[11], Data[12], Data[13], Data[14], Data[15]}),
    .en(decoder_1_out2), .Q(Col_2), .clk(CLOCK), .clr(RESET));
  Register #(.width(16)) register_4 (
    .D({Data[0], Data[1], Data[2], Data[3], Data[4], Data[5], Data[6], Data[7], Data[8], Data[9], Data[10], Data[11], Data[12], Data[13], Data[14], Data[15]}),
    .en(decoder_1_out3), .Q(Col_3), .clk(CLOCK), .clr(RESET));
  Register #(.width(16)) register_5 (
    .D({Data[0], Data[1], Data[2], Data[3], Data[4], Data[5], Data[6], Data[7], Data[8], Data[9], Data[10], Data[11], Data[12], Data[13], Data[14], Data[15]}),
    .en(decoder_1_out4), .Q(Col_4), .clk(CLOCK), .clr(RESET));
  Register #(.width(16)) register_6 (
    .D({Data[0], Data[1], Data[2], Data[3], Data[4], Data[5], Data[6], Data[7], Data[8], Data[9], Data[10], Data[11], Data[12], Data[13], Data[14], Data[15]}),
    .en(decoder_1_out5), .Q(Col_5), .clk(CLOCK), .clr(RESET));
  Register #(.width(16)) register_7 (
    .D({Data[0], Data[1], Data[2], Data[3], Data[4], Data[5], Data[6], Data[7], Data[8], Data[9], Data[10], Data[11], Data[12], Data[13], Data[14], Data[15]}),
    .en(decoder_1_out6), .Q(Col_6), .clk(CLOCK), .clr(RESET));
  Register #(.width(16)) register_8 (
    .D({Data[0], Data[1], Data[2], Data[3], Data[4], Data[5], Data[6], Data[7], Data[8], Data[9], Data[10], Data[11], Data[12], Data[13], Data[14], Data[15]}),
    .en(decoder_1_out7), .Q(Col_7), .clk(CLOCK), .clr(RESET));
  Register #(.width(16)) register_9 (
    .D({Data[0], Data[1], Data[2], Data[3], Data[4], Data[5], Data[6], Data[7], Data[8], Data[9], Data[10], Data[11], Data[12], Data[13], Data[14], Data[15]}),
    .en(decoder_1_out8), .Q(Col_8), .clk(CLOCK), .clr(RESET));
  Register #(.width(16)) register_10 (
    .D({Data[0], Data[1], Data[2], Data[3], Data[4], Data[5], Data[6], Data[7], Data[8], Data[9], Data[10], Data[11], Data[12], Data[13], Data[14], Data[15]}),
    .en(decoder_1_out9), .Q(Col_9), .clk(CLOCK), .clr(RESET));
  Register #(.width(16)) register_11 (
    .D({Data[0], Data[1], Data[2], Data[3], Data[4], Data[5], Data[6], Data[7], Data[8], Data[9], Data[10], Data[11], Data[12], Data[13], Data[14], Data[15]}),
    .en(decoder_1_out10), .Q(Col_10), .clk(CLOCK), .clr(RESET));
  Register #(.width(16)) register_12 (
    .D({Data[0], Data[1], Data[2], Data[3], Data[4], Data[5], Data[6], Data[7], Data[8], Data[9], Data[10], Data[11], Data[12], Data[13], Data[14], Data[15]}),
    .en(decoder_1_out11), .Q(Col_11), .clk(CLOCK), .clr(RESET));
  Register #(.width(16)) register_13 (
    .D({Data[0], Data[1], Data[2], Data[3], Data[4], Data[5], Data[6], Data[7], Data[8], Data[9], Data[10], Data[11], Data[12], Data[13], Data[14], Data[15]}),
    .en(decoder_1_out12), .Q(Col_12), .clk(CLOCK), .clr(RESET));
  Register #(.width(16)) register_14 (
    .D({Data[0], Data[1], Data[2], Data[3], Data[4], Data[5], Data[6], Data[7], Data[8], Data[9], Data[10], Data[11], Data[12], Data[13], Data[14], Data[15]}),
    .en(decoder_1_out13), .Q(Col_13), .clk(CLOCK), .clr(RESET));
  Register #(.width(16)) register_15 (
    .D({Data[0], Data[1], Data[2], Data[3], Data[4], Data[5], Data[6], Data[7], Data[8], Data[9], Data[10], Data[11], Data[12], Data[13], Data[14], Data[15]}),
    .en(decoder_1_out14), .Q(Col_14), .clk(CLOCK), .clr(RESET));
  Register #(.width(16)) register_16 (
    .D({Data[0], Data[1], Data[2], Data[3], Data[4], Data[5], Data[6], Data[7], Data[8], Data[9], Data[10], Data[11], Data[12], Data[13], Data[14], Data[15]}),
    .en(decoder_1_out15), .Q(Col_15), .clk(CLOCK), .clr(RESET));
  Register #(.width(16)) register_17 (
    .D({Data[0], Data[1], Data[2], Data[3], Data[4], Data[5], Data[6], Data[7], Data[8], Data[9], Data[10], Data[11], Data[12], Data[13], Data[14], Data[15]}),
    .en(decoder_1_out16), .Q(Col_16), .clk(CLOCK), .clr(RESET));
  Register #(.width(16)) register_18 (
    .D({Data[0], Data[1], Data[2], Data[3], Data[4], Data[5], Data[6], Data[7], Data[8], Data[9], Data[10], Data[11], Data[12], Data[13], Data[14], Data[15]}),
    .en(decoder_1_out17), .Q(Col_17), .clk(CLOCK), .clr(RESET));
  Register #(.width(16)) register_19 (
    .D({Data[0], Data[1], Data[2], Data[3], Data[4], Data[5], Data[6], Data[7], Data[8], Data[9], Data[10], Data[11], Data[12], Data[13], Data[14], Data[15]}),
    .en(decoder_1_out18), .Q(Col_18), .clk(CLOCK), .clr(RESET));
  Register #(.width(16)) register_20 (
    .D({Data[0], Data[1], Data[2], Data[3], Data[4], Data[5], Data[6], Data[7], Data[8], Data[9], Data[10], Data[11], Data[12], Data[13], Data[14], Data[15]}),
    .en(decoder_1_out19), .Q(Col_19), .clk(CLOCK), .clr(RESET));
  Register #(.width(16)) register_21 (
    .D({Data[0], Data[1], Data[2], Data[3], Data[4], Data[5], Data[6], Data[7], Data[8], Data[9], Data[10], Data[11], Data[12], Data[13], Data[14], Data[15]}),
    .en(decoder_1_out20), .Q(Col_20), .clk(CLOCK), .clr(RESET));
  Register #(.width(16)) register_22 (
    .D({Data[0], Data[1], Data[2], Data[3], Data[4], Data[5], Data[6], Data[7], Data[8], Data[9], Data[10], Data[11], Data[12], Data[13], Data[14], Data[15]}),
    .en(decoder_1_out21), .Q(Col_21), .clk(CLOCK), .clr(RESET));
  Register #(.width(16)) register_23 (
    .D({Data[0], Data[1], Data[2], Data[3], Data[4], Data[5], Data[6], Data[7], Data[8], Data[9], Data[10], Data[11], Data[12], Data[13], Data[14], Data[15]}),
    .en(decoder_1_out22), .Q(Col_22), .clk(CLOCK), .clr(RESET));
  Register #(.width(16)) register_24 (
    .D({Data[0], Data[1], Data[2], Data[3], Data[4], Data[5], Data[6], Data[7], Data[8], Data[9], Data[10], Data[11], Data[12], Data[13], Data[14], Data[15]}),
    .en(decoder_1_out23), .Q(Col_23), .clk(CLOCK), .clr(RESET));
  Register #(.width(16)) register_25 (
    .D({Data[0], Data[1], Data[2], Data[3], Data[4], Data[5], Data[6], Data[7], Data[8], Data[9], Data[10], Data[11], Data[12], Data[13], Data[14], Data[15]}),
    .en(decoder_1_out24), .Q(Col_24), .clk(CLOCK), .clr(RESET));
  Register #(.width(16)) register_26 (
    .D({Data[0], Data[1], Data[2], Data[3], Data[4], Data[5], Data[6], Data[7], Data[8], Data[9], Data[10], Data[11], Data[12], Data[13], Data[14], Data[15]}),
    .en(decoder_1_out25), .Q(Col_25), .clk(CLOCK), .clr(RESET));
  Register #(.width(16)) register_27 (
    .D({Data[0], Data[1], Data[2], Data[3], Data[4], Data[5], Data[6], Data[7], Data[8], Data[9], Data[10], Data[11], Data[12], Data[13], Data[14], Data[15]}),
    .en(decoder_1_out26), .Q(Col_26), .clk(CLOCK), .clr(RESET));
  Register #(.width(16)) register_28 (
    .D({Data[0], Data[1], Data[2], Data[3], Data[4], Data[5], Data[6], Data[7], Data[8], Data[9], Data[10], Data[11], Data[12], Data[13], Data[14], Data[15]}),
    .en(decoder_1_out27), .Q(Col_27), .clk(CLOCK), .clr(RESET));
  Register #(.width(16)) register_29 (
    .D({Data[0], Data[1], Data[2], Data[3], Data[4], Data[5], Data[6], Data[7], Data[8], Data[9], Data[10], Data[11], Data[12], Data[13], Data[14], Data[15]}),
    .en(decoder_1_out28), .Q(Col_28), .clk(CLOCK), .clr(RESET));
  Register #(.width(16)) register_30 (
    .D({Data[0], Data[1], Data[2], Data[3], Data[4], Data[5], Data[6], Data[7], Data[8], Data[9], Data[10], Data[11], Data[12], Data[13], Data[14], Data[15]}),
    .en(decoder_1_out29), .Q(Col_29), .clk(CLOCK), .clr(RESET));
  Register #(.width(16)) register_31 (
    .D({Data[0], Data[1], Data[2], Data[3], Data[4], Data[5], Data[6], Data[7], Data[8], Data[9], Data[10], Data[11], Data[12], Data[13], Data[14], Data[15]}),
    .en(decoder_1_out30), .Q(Col_30), .clk(CLOCK), .clr(RESET));
  Register #(.width(16)) register_32 (
    .D({Data[0], Data[1], Data[2], Data[3], Data[4], Data[5], Data[6], Data[7], Data[8], Data[9], Data[10], Data[11], Data[12], Data[13], Data[14], Data[15]}),
    .en(decoder_1_out31), .Q(Col_31), .clk(CLOCK), .clr(RESET));

  // Notes on the sheet:
  //   CLOCK: pull=down
  //   Enable: pull=up
  //   Adress: pull=down
  //   Data: pull=down
  //   RESET: pull=down
  //   Mapped address
endmodule

module Button_inputs (
  input  Left,
  input  Up,
  input  Down,
  input  Right,
  input  Start,
  input  Select,
  input  X,
  input  A,
  input  Y,
  input  B,
  input  Clock,
  input  Clear_interrupt,
  input  Reset,
  output [15:0] Data_out,
  output Interrupt
);

  wire and_1_out, comparator_1_eq, or_1_out;
  wire [15:0] register_1_q;

  Pull_Resistor pull_resistor_1 (.node({Data_out[15:10], Select, Start, B, A, Y, X, Right, Down, Up, Left}));
  and and_1 (and_1_out, Clock, Clear_interrupt, Reset);
  or or_1 (or_1_out, and_1_out, Reset);
  Comparator #(.width(16)) comparator_1 (
    .a({Data_out[15:10], Select, Start, B, A, Y, X, Right, Down, Up, Left}), .b(register_1_q),
    .eq(comparator_1_eq));  // open: gt, lt
  Register #(.width(16)) register_1 (
    .D({Data_out[15:10], Select, Start, B, A, Y, X, Right, Down, Up, Left}), .Q(register_1_q), .clk(or_1_out));  // open: en, clr
  not not_1 (Interrupt, comparator_1_eq);

  assign Data_out[9:0] = {Select, Start, B, A, Y, X, Right, Down, Up, Left};
endmodule
