// Logisim project testing.circ as structural Verilog: 3 circuits, main circuit main
module main (
);

  wire adder_2_cout, and_3_p5, Auto_out, clock_2_out, Clock_3_out, Clock_out, comparator_1_eq,
       comparator_1_lt, comparator_2_eq, comparator_2_gt, comparator_3_eq, comparator_3_lt, comparator_4_eq,
       comparator_4_gt, comparator_4_lt, comparator_5_gt, comparator_6_eq, Manual_out, multiplexer_3_out,
       not_1_out, not_2_out, not_3_out, not_4_out, or_1_out, or_2_p2, or_2_p3, or_3_p1, or_3_p4, or_4_out,
       or_5_out, Reset_2_out, Reset_3_out, Reset_out, subtractor_1_bout;
  wire [0:0] Divisor_Low_2_q, Divisor_Low_q;
  wire [4:0] bit_extender_1_out, bit_extender_2_out;
  wire [5:0] Limit_2_q, pull_resistor_4_node;
  wire [30:0] Divisor_High_2_q, Divisor_High_q, Divisor_Low_2_q_2, Divisor_Low_q_2;
  wire [31:0] Accumulator_q, adder_1_out, adder_2_out, and_2_out, Limit_3_q, Limit_q, Mask_q,
       multiplexer_1_out, multiplexer_2_out, multiplexer_4_out, negator_1_out, not_5_out,
       pull_resistor_1_node, pull_resistor_2_node, pull_resistor_3_node, pull_resistor_5_node,
       pull_resistor_6_node, Remainder_2_q, Remainder_q, shifter_1_out, shifter_2_out, subtractor_1_out,
       Value_q;
  wire [31:1] undriven;
  wire [31:31] Accumulator_2_q, Accumulator_3_q, undriven_2;

  Button Reset (.out(Reset_out));
  Button Clock (.out(Clock_out));
  Register #(.width(32)) Accumulator (.D(adder_1_out), .en(1'b1), .Q(Accumulator_q), .clk(Clock_out), .clr(Reset_out));
  Register #(.width(32)) Value (.D(shifter_1_out), .en(1'b1), .Q(Value_q), .clk(Clock_out), .clr(Reset_out));
  Register #(.width(32)) Mask (.D(shifter_2_out), .en(1'b1), .Q(Mask_q), .clk(Clock_out), .clr(Reset_out));
  Counter #(.width(32), .max('hffffffff)) Limit (
    .load(1'b1), .count(1'b0), .Q(Limit_q), .clk(Clock_out), .clr(Reset_out));  // open: D, carry
  Pull_Resistor pull_resistor_1 (.node(pull_resistor_1_node));
  assign pull_resistor_1_node = 1'b1 ? Accumulator_q : 32'bz;  // Controlled_Buffer controlled_buffer_1
  Pull_Resistor pull_resistor_2 (.node(pull_resistor_2_node));
  assign pull_resistor_2_node = Mask_q[0] ? Value_q : 32'bz;  // Controlled_Buffer controlled_buffer_2
  Adder #(.width(32)) adder_1 (
    .a(pull_resistor_1_node), .b(pull_resistor_2_node), .out(adder_1_out));  // open: cin, cout
  Shifter #(.width(32)) shifter_1 (.in(Value_q), .\dist (bit_extender_1_out), .out(shifter_1_out));
  assign bit_extender_1_out = {{4{1'b0}}, 1'b1};  // Bit_Extender bit_extender_1
  Shifter #(.width(32), .shift("lr")) shifter_2 (.in(Mask_q), .\dist (bit_extender_2_out), .out(shifter_2_out));
  assign bit_extender_2_out = {{4{1'b0}}, 1'b1};  // Bit_Extender bit_extender_2
  Comparator #(.width(32), .mode("unsigned")) comparator_1 (
    .a(Mask_q), .b({32{1'b0}}), .eq(comparator_1_eq), .lt(comparator_1_lt));  // open: gt
  or or_1 (or_1_out, comparator_1_eq, comparator_1_lt, comparator_2_gt, comparator_2_eq);
  Comparator #(.width(32), .mode("unsigned")) comparator_2 (
    .a(Limit_q), .b({32{1'b0}}), .gt(comparator_2_gt), .eq(comparator_2_eq));  // open: lt
  LED Done (.in(or_1_out));
  Button Reset_2 (.out(Reset_2_out));
  Button Manual (.out(Manual_out));
  Button Auto (.out(Auto_out));
  Clock clock_2 (.out(clock_2_out));
  Register #(.width(32)) Accumulator_2 (
    .D(and_2_out), .en(1'b1), .Q({Accumulator_2_q[31], and_2_out[31:1]}), .clk(or_2_p2), .clr(Reset_2_out));
  Register #(.width(32)) Remainder (
    .D(multiplexer_1_out), .en(1'b1), .Q(Remainder_q), .clk(or_2_p2), .clr(Reset_2_out));
  Register #(.width(31)) Divisor_Low (
    .D(Divisor_Low_q_2), .en(1'b1), .Q({Divisor_Low_q_2[29:0], Divisor_Low_q[0]}), .clk(or_2_p2),
    .clr(Reset_2_out));
  Register #(.width(32)) Divisor_High (
    .D({1'b0, Divisor_High_q}), .en(1'b1), .Q({Divisor_High_q, Divisor_Low_q_2[30]}), .clk(or_2_p2),
    .clr(Reset_2_out));
  Counter #(.width(6), .max('h3f)) Limit_2 (
    .load(1'b1), .count(1'b1), .Q(Limit_2_q), .clk(or_2_p2), .clr(Reset_2_out));  // open: D, carry
  // OR_Gate or_2: pin names not known; wires that end beside it: Manual_out, or_2_p2, or_2_p3
  and and_1 (or_2_p3, ~or_4_out, clock_2_out, Auto_out);  // AND_Gate
  and and_2 (and_2_out[0], not_1_out, 1'b1);
  Multiplexer #(.width(32)) multiplexer_1 (
    .in0(adder_2_out), .in1(Remainder_q), .out(multiplexer_1_out), .sel(multiplexer_3_out));  // open: en
  not not_1 (not_1_out, multiplexer_3_out);
  Multiplexer #(.width(32)) multiplexer_2 (
    .in0({Accumulator_2_q[31], and_2_out[31:1]}), .in1(negator_1_out), .out(multiplexer_2_out), .sel(1'b1));  // open: en
  Negator #(.width(32)) negator_1 (.in({Divisor_Low_q_2, Divisor_Low_q[0]}), .out(negator_1_out));
  Pull_Resistor pull_resistor_3 (.node(pull_resistor_3_node));
  Pull_Resistor pull_resistor_4 (.node(pull_resistor_4_node));
  not not_2 (not_2_out, adder_2_cout);
  // OR_Gate or_3: pin names not known; wires that end beside it: or_3_p1, not_2_out, not_2_out, or_3_p4
  Multiplexer multiplexer_3 (.in0(or_3_p1), .in1(not_4_out), .out(multiplexer_3_out), .sel(not_3_out));  // open: en
  not not_3 (not_3_out, 1'b1);
  not not_4 (not_4_out, Divisor_Low_q_2[30]);
  Comparator #(.width(32), .mode("unsigned")) comparator_3 (
    .a({Divisor_High_q, Divisor_Low_q_2[30]}), .b(pull_resistor_3_node), .gt(or_3_p4), .eq(comparator_3_eq),
    .lt(comparator_3_lt));
  // AND_Gate and_3: pin names not known; wires that end beside it: or_3_p4, comparator_3_lt, 1'b1, comparator_3_eq, and_3_p5
  or or_4 (or_4_out, comparator_4_gt, comparator_4_eq, comparator_4_lt);
  Comparator #(.width(6), .mode("unsigned")) comparator_4 (
    .a(Limit_2_q), .b(pull_resistor_4_node), .gt(comparator_4_gt), .eq(comparator_4_eq), .lt(comparator_4_lt));
  Adder #(.width(32)) adder_2 (
    .a(Remainder_q), .b(multiplexer_2_out), .out(adder_2_out), .cout(adder_2_cout));  // open: cin
  LED Done_2 (.in(or_4_out));
  Button Reset_3 (.out(Reset_3_out));
  Button Clock_3 (.out(Clock_3_out));
  Register #(.width(32)) Accumulator_3 (
    .D(not_5_out), .en(1'b1), .Q({Accumulator_3_q[31], not_5_out[31:1]}), .clk(Clock_3_out), .clr(Reset_3_out));
  Register #(.width(32)) Remainder_2 (
    .D(multiplexer_4_out), .en(1'b1), .Q(Remainder_2_q), .clk(Clock_3_out), .clr(Reset_3_out));
  Register #(.width(31)) Divisor_Low_2 (
    .D(Divisor_Low_2_q_2), .en(1'b1), .Q({Divisor_Low_2_q_2[29:0], Divisor_Low_2_q[0]}), .clk(Clock_3_out),
    .clr(Reset_3_out));
  Register #(.width(32)) Divisor_High_2 (
    .D({1'b0, Divisor_High_2_q}), .en(1'b1), .Q({Divisor_High_2_q, Divisor_Low_2_q_2[30]}),
    .clk(Clock_3_out), .clr(Reset_3_out));
  Counter #(.width(32), .max('hffffffff)) Limit_3 (
    .load(1'b1), .count(1'b1), .Q(Limit_3_q), .clk(Clock_3_out), .clr(Reset_3_out));  // open: D, carry
  Multiplexer #(.width(32)) multiplexer_4 (
    .in0(subtractor_1_out), .in1(Remainder_2_q), .out(multiplexer_4_out), .sel(or_5_out));  // open: en
  not not_5 (not_5_out[0], or_5_out);
  or or_5 (or_5_out, subtractor_1_bout, comparator_5_gt);
  Comparator #(.width(32), .mode("unsigned")) comparator_5 (
    .a({Divisor_High_2_q, Divisor_Low_2_q_2[30]}), .b(pull_resistor_5_node), .gt(comparator_5_gt));  // open: eq, lt
  Pull_Resistor pull_resistor_5 (.node(pull_resistor_5_node));
  Comparator #(.width(32), .mode("unsigned")) comparator_6 (
    .a(Limit_3_q), .b(pull_resistor_6_node), .eq(comparator_6_eq));  // open: gt, lt
  Pull_Resistor pull_resistor_6 (.node(pull_resistor_6_node));
  Multiplexer #(.width(32)) multiplexer_5 (
    .in0({undriven, 1'b0}), .in1({undriven_2[31], undriven}));  // open: out, sel, en
  Subtractor #(.width(32)) subtractor_1 (
    .a(Remainder_2_q), .b({Divisor_Low_2_q_2, Divisor_Low_2_q[0]}), .out(subtractor_1_out),
    .bout(subtractor_1_bout));  // open: bin
  LED Done_3 (.in(comparator_6_eq));

  // Notes on the sheet:
  //   Enable
  //   1 Div / 0 Mul
endmodule

module An_double_dabbler (
  input  [15:0] D,
  input  Write_Enable,
  input  Clock,
  output [15:0] Q
);

  wire [15:0] register_1_q;

  Register #(.width(16)) register_1 (.D(D), .en(Write_Enable), .Q(register_1_q), .clk(Clock));  // open: clr
  nibbles_of_dabbles_doubler nibbles_of_dabbles_doubler_1 (.A(register_1_q[3:0]), .Q(Q[3:0]));
  nibbles_of_dabbles_doubler nibbles_of_dabbles_doubler_2 (.A(register_1_q[7:4]), .Q(Q[7:4]));
  nibbles_of_dabbles_doubler nibbles_of_dabbles_doubler_3 (.A(register_1_q[11:8]), .Q(Q[11:8]));
  nibbles_of_dabbles_doubler nibbles_of_dabbles_doubler_4 (.A(register_1_q[15:12]), .Q(Q[15:12]));
endmodule

module nibbles_of_dabbles_doubler (
  input  [3:0] A,
  output [3:0] Q
);

  wire and_1_p3, or_1_p3;
  wire [1:1] or_2_out;

  // OR_Gate or_1: pin names not known; wires that end beside it: A[0], A[1], or_1_p3
  // AND_Gate and_1: pin names not known; wires that end beside it: or_1_p3, A[2], and_1_p3
  or or_2 (or_2_out[1], and_1_p3, A[3]);
  Adder #(.width(4)) adder_1 (.a({2'b00, {2{or_2_out[1]}}}), .b(A), .out(Q));  // open: cin, cout
endmodule
